// Logisim project 10x7.circ as structural Verilog: 2 circuits, main circuit main
module main (
  input  one,
  input  two,
  input  three,
  input  four,
  input  five,
  input  six,
  input  seven,
  input  eight,
  input  nine,
  input  zero
);

  wire or_1_out, or_2_out, or_3_out, or_4_out, or_5_out, or_6_out, or_7_out, or_8_out, or_9_out, or_10_out,
       or_11_out, or_12_out, or_13_out, or_14_out, or_15_out, or_16_out, or_17_out, or_18_out, or_19_out,
       or_20_out, or_21_out, or_22_out, or_23_out, or_24_out, or_25_out, or_26_out, or_27_out, or_28_out,
       or_29_out, or_30_out, or_31_out, or_32_out, or_33_out, or_34_out, or_35_out, or_36_out, or_37_out,
       or_38_out, or_39_out, or_40_out, or_41_out;

  or or_1 (or_1_out, two, three);
  or or_2 (or_2_out, five, seven);
  or or_3 (or_3_out, eight, nine);
  or or_4 (or_4_out, zero, six);
  or or_5 (or_5_out, one, two);
  or or_6 (or_6_out, three, four);
  or or_7 (or_7_out, seven, eight);
  or or_8 (or_8_out, nine, zero);
  or or_9 (or_9_out, one, three);
  or or_10 (or_10_out, four, five);
  or or_11 (or_11_out, six, seven);
  or or_12 (or_12_out, eight, nine);
  or or_13 (or_13_out, two, three);
  or or_14 (or_14_out, five, six);
  or or_15 (or_15_out, eight, zero);
  or or_16 (or_16_out, two, six);
  or or_17 (or_17_out, eight, zero);
  or or_18 (or_18_out, four, five);
  or or_19 (or_19_out, six, eight);
  or or_20 (or_20_out, nine, zero);
  or or_21 (or_21_out, two, three);
  or or_22 (or_22_out, four, five);
  or or_23 (or_23_out, six, eight);
  or or_24 (or_24_out, or_1_out, or_2_out);
  or or_25 (or_25_out, or_24_out, or_26_out);
  or or_26 (or_26_out, or_3_out, or_4_out);
  or or_27 (or_27_out, or_5_out, or_6_out);
  or or_28 (or_28_out, or_27_out, or_29_out);
  or or_29 (or_29_out, or_7_out, or_8_out);
  or or_30 (or_30_out, or_9_out, or_10_out);
  or or_31 (or_31_out, or_30_out, or_32_out);
  or or_32 (or_32_out, or_11_out, or_12_out);
  or or_33 (or_33_out, or_13_out, or_14_out);
  or or_34 (or_34_out, or_33_out, or_15_out);
  or or_35 (or_35_out, or_16_out, or_17_out);
  or or_36 (or_36_out, or_18_out, or_19_out);
  or or_37 (or_37_out, or_36_out, or_20_out);
  or or_38 (or_38_out, or_21_out, or_22_out);
  or or_39 (or_39_out, or_38_out, or_40_out);
  or or_40 (or_40_out, or_23_out, nine);
  or or_41 (or_41_out, or_31_out, zero);
  _7_Segment_Display #(.decimalPoint("false")) u_7_segment_display_1 (
    .g(or_39_out), .f(or_37_out), .a(or_25_out), .b(or_28_out), .e(or_35_out), .d(or_34_out), .c(or_41_out));

  // Notes on the sheet:
  //   Segment  A
  //   Segment  C
  //   Segment  D
  //   Segment  E
  //   Segment  F
  //   Segment  G
  //   Segment  B
endmodule

module optimized (
  input  one,
  input  two,
  input  three,
  input  four,
  input  five,
  input  six,
  input  seven,
  input  eight,
  input  nine,
  input  zero
);

  wire nand_1_out, nand_2_out, nand_3_out, nand_4_out, nor_1_out, nor_2_out, nor_3_out, nor_4_out, nor_5_out,
       nor_6_out, nor_7_out, or_1_out, or_2_out, or_3_out, or_4_out, or_5_out, or_6_out, or_7_out, or_8_out,
       or_9_out, or_10_out;

  nor nor_1 (nor_1_out, one, three);
  nor nor_2 (nor_2_out, three, two);
  or or_1 (or_1_out, four, one);
  or or_2 (or_2_out, five, four);
  nor nor_3 (nor_3_out, six, two);
  or or_3 (or_3_out, five, three);
  nor nor_4 (nor_4_out, eight, zero);
  nor nor_5 (nor_5_out, nine, eight);
  or or_4 (or_4_out, zero, seven);
  or or_5 (or_5_out, or_2_out, six);
  nand nand_1 (nand_1_out, nor_3_out, nor_4_out);
  nand nand_2 (nand_2_out, nor_2_out, nor_5_out);
  nor nor_6 (nor_6_out, or_5_out, zero);
  or or_6 (or_6_out, or_3_out, nand_1_out);
  or or_7 (or_7_out, nand_2_out, or_5_out);
  or or_8 (or_8_out, nand_2_out, or_4_out);
  or or_9 (or_9_out, or_8_out, or_1_out);
  nand nand_3 (nand_3_out, nor_5_out, nor_6_out);
  or or_10 (or_10_out, or_8_out, five);
  nor nor_7 (nor_7_out, nand_3_out, seven);
  nand nand_4 (nand_4_out, nor_1_out, nor_7_out);
  _7_Segment_Display #(.decimalPoint("false")) u_7_segment_display_1 (
    .g(or_7_out), .f(nand_3_out), .a(or_10_out), .b(or_9_out), .e(nand_1_out), .d(or_6_out), .c(nand_4_out));
endmodule
