// Logisim project 10x7onlySegA.circ as structural Verilog: 1 circuit, main circuit main
module main (
  input  one,
  input  two,
  input  three,
  input  four,
  input  five,
  input  six,
  input  seven,
  input  eight,
  input  nine,
  input  zero
);

  wire or_1_out, or_2_out, or_3_out, or_5_out, or_7_out;

  or or_1 (or_1_out, two, three);
  or or_2 (or_2_out, six, seven);
  or or_3 (or_3_out, eight, nine);
  // OR_Gate or_4 is placed but not wired
  or or_5 (or_5_out, or_1_out, or_2_out);
  // OR_Gate or_6 has open pins: in0=or_5_out, in1=or_7_out, out=open
  or or_7 (or_7_out, or_3_out, zero);
  _7_Segment_Display #(.decimalPoint("false")) u_7_segment_display_1 ();  // open: g, f, a, b, e, d, c

  // Notes on the sheet:
  //   Segment  A
endmodule
