// Logisim project 7segDecoder.circ as structural Verilog: 10 circuits, main circuit seg7_10in
module segA_10in (
  input  one,
  input  two,
  input  three,
  input  four,
  input  five,
  input  six,
  input  seven,
  input  eight,
  input  nine,
  input  zero
);

  wire or_1_out, or_2_out, or_3_out, or_5_out, or_7_out;

  or or_1 (or_1_out, two, three);
  or or_2 (or_2_out, six, seven);
  or or_3 (or_3_out, eight, nine);
  // OR_Gate or_4 is placed but not wired
  or or_5 (or_5_out, or_1_out, or_2_out);
  // OR_Gate or_6 has open pins: in0=or_5_out, in1=or_7_out, out=open
  or or_7 (or_7_out, or_3_out, zero);
  _7_Segment_Display #(.decimalPoint("false")) u_7_segment_display_1 ();  // open: g, f, a, b, e, d, c

  // Notes on the sheet:
  //   Segment  A
endmodule

module seg7_10in (
  input  one,
  input  two,
  input  three,
  input  four,
  input  five,
  input  six,
  input  seven,
  input  eight,
  input  nine,
  input  zero
);

  wire or_1_out, or_2_out, or_3_out, or_4_out, or_5_out, or_6_out, or_7_out, or_8_out, or_9_out, or_10_out,
       or_11_out, or_12_out, or_13_out, or_14_out, or_15_out, or_16_out, or_17_out, or_18_out, or_19_out,
       or_20_out, or_21_out, or_22_out, or_23_out, or_24_out, or_25_out, or_26_out, or_27_out, or_28_out,
       or_29_out, or_30_out, or_31_out, or_32_out, or_33_out, or_34_out, or_35_out, or_36_out, or_37_out,
       or_38_out, or_39_out, or_40_out, or_41_out;

  or or_1 (or_1_out, two, three);
  or or_2 (or_2_out, five, seven);
  or or_3 (or_3_out, eight, nine);
  or or_4 (or_4_out, zero, six);
  or or_5 (or_5_out, one, two);
  or or_6 (or_6_out, three, four);
  or or_7 (or_7_out, seven, eight);
  or or_8 (or_8_out, nine, zero);
  or or_9 (or_9_out, one, three);
  or or_10 (or_10_out, four, five);
  or or_11 (or_11_out, six, seven);
  or or_12 (or_12_out, eight, nine);
  or or_13 (or_13_out, two, three);
  or or_14 (or_14_out, five, six);
  or or_15 (or_15_out, eight, zero);
  or or_16 (or_16_out, two, six);
  or or_17 (or_17_out, eight, zero);
  or or_18 (or_18_out, four, five);
  or or_19 (or_19_out, six, eight);
  or or_20 (or_20_out, nine, zero);
  or or_21 (or_21_out, two, three);
  or or_22 (or_22_out, four, five);
  or or_23 (or_23_out, six, eight);
  or or_24 (or_24_out, or_1_out, or_2_out);
  or or_25 (or_25_out, or_24_out, or_26_out);
  or or_26 (or_26_out, or_3_out, or_4_out);
  or or_27 (or_27_out, or_5_out, or_6_out);
  or or_28 (or_28_out, or_27_out, or_29_out);
  or or_29 (or_29_out, or_7_out, or_8_out);
  or or_30 (or_30_out, or_9_out, or_10_out);
  or or_31 (or_31_out, or_30_out, or_32_out);
  or or_32 (or_32_out, or_11_out, or_12_out);
  or or_33 (or_33_out, or_13_out, or_14_out);
  or or_34 (or_34_out, or_33_out, or_15_out);
  or or_35 (or_35_out, or_16_out, or_17_out);
  or or_36 (or_36_out, or_18_out, or_19_out);
  or or_37 (or_37_out, or_36_out, or_20_out);
  or or_38 (or_38_out, or_21_out, or_22_out);
  or or_39 (or_39_out, or_38_out, or_40_out);
  or or_40 (or_40_out, or_23_out, nine);
  or or_41 (or_41_out, or_31_out, zero);
  _7_Segment_Display #(.decimalPoint("false")) u_7_segment_display_1 (
    .g(or_39_out), .f(or_37_out), .a(or_25_out), .b(or_28_out), .e(or_35_out), .d(or_34_out), .c(or_41_out));

  // Notes on the sheet:
  //   Segment  A
  //   Segment  C
  //   Segment  D
  //   Segment  E
  //   Segment  F
  //   Segment  G
  //   Segment  B
endmodule

module decoder_x4_uncompact (
  input  x0,
  input  x1,
  input  x2,
  input  x3,
  output d0,
  output d1,
  output d2,
  output d3,
  output d4,
  output d5,
  output d6,
  output d7,
  output d8,
  output d9,
  output d10,
  output out_16,
  output out_17,
  output out_18,
  output out_19,
  output out_20
);

  wire and_1_out, and_2_out, and_3_out, and_4_out, and_5_out, and_6_out, and_7_out, and_8_out, and_9_out,
       and_10_out, and_11_out, and_12_out, and_13_out, and_14_out, and_15_out, and_16_out, and_17_out,
       and_18_out, and_19_out, and_20_out, and_21_out, and_22_out, and_23_out, and_24_out, and_25_out,
       and_26_out, and_27_out, and_28_out, and_29_out, and_30_out, and_31_out, and_32_out, not_1_out,
       not_2_out, not_3_out, not_4_out;

  not not_1 (not_1_out, x0);
  not not_2 (not_2_out, x1);
  not not_3 (not_3_out, x2);
  not not_4 (not_4_out, x3);
  and and_1 (and_1_out, not_1_out, not_2_out);
  and and_2 (and_2_out, not_3_out, not_4_out);
  and and_3 (and_3_out, x0, not_2_out);
  and and_4 (and_4_out, not_3_out, not_4_out);
  and and_5 (and_5_out, not_1_out, x1);
  and and_6 (and_6_out, not_3_out, not_4_out);
  and and_7 (and_7_out, x0, x1);
  and and_8 (and_8_out, not_3_out, not_4_out);
  and and_9 (and_9_out, x2, not_1_out);
  and and_10 (and_10_out, not_2_out, not_4_out);
  and and_11 (and_11_out, x0, x2);
  and and_12 (and_12_out, not_2_out, not_4_out);
  and and_13 (and_13_out, x2, x1);
  and and_14 (and_14_out, not_1_out, not_4_out);
  and and_15 (and_15_out, x0, x1);
  and and_16 (and_16_out, x2, not_4_out);
  and and_17 (and_17_out, not_1_out, not_2_out);
  and and_18 (and_18_out, not_3_out, x3);
  and and_19 (and_19_out, x0, x3);
  and and_20 (and_20_out, not_2_out, not_3_out);
  and and_21 (and_21_out, x1, x3);
  and and_22 (and_22_out, not_1_out, not_3_out);
  and and_23 (and_23_out, x3, x1);
  and and_24 (and_24_out, x0, not_3_out);
  and and_25 (and_25_out, x3, x2);
  and and_26 (and_26_out, not_1_out, not_2_out);
  and and_27 (and_27_out, x3, x2);
  and and_28 (and_28_out, x0, not_2_out);
  and and_29 (and_29_out, x3, x2);
  and and_30 (and_30_out, x1, not_1_out);
  and and_31 (and_31_out, x3, x2);
  and and_32 (and_32_out, x1, x0);
  and and_33 (d0, and_1_out, and_2_out);
  and and_34 (d1, and_3_out, and_4_out);
  and and_35 (d2, and_5_out, and_6_out);
  and and_36 (d3, and_7_out, and_8_out);
  and and_37 (d4, and_9_out, and_10_out);
  and and_38 (d5, and_11_out, and_12_out);
  and and_39 (d6, and_13_out, and_14_out);
  and and_40 (d7, and_15_out, and_16_out);
  and and_41 (d8, and_17_out, and_18_out);
  and and_42 (d9, and_19_out, and_20_out);
  and and_43 (d10, and_21_out, and_22_out);
  and and_44 (out_16, and_23_out, and_24_out);
  and and_45 (out_17, and_25_out, and_26_out);
  and and_46 (out_18, and_27_out, and_28_out);
  and and_47 (out_19, and_29_out, and_30_out);
  and and_48 (out_20, and_31_out, and_32_out);
endmodule

module decoder_x1 (
  input  i,
  output o0,
  output o1
);

  not not_1 (o0, i);

  assign o1 = i;
endmodule

module decoder_x2 (
  input  [1:0] i,
  output o0,
  output o1,
  output o2,
  output o3
);

  wire decoder_x1_1_o0, decoder_x1_1_o1, decoder_x1_2_o0, decoder_x1_2_o1;

  decoder_x1 decoder_x1_1 (.i(i[0]), .o0(decoder_x1_1_o0), .o1(decoder_x1_1_o1));
  decoder_x1 decoder_x1_2 (.i(i[1]), .o0(decoder_x1_2_o0), .o1(decoder_x1_2_o1));
  and and_1 (o0, decoder_x1_1_o0, decoder_x1_2_o0);
  and and_2 (o1, decoder_x1_1_o1, decoder_x1_2_o0);
  and and_3 (o2, decoder_x1_1_o0, decoder_x1_2_o1);
  and and_4 (o3, decoder_x1_1_o1, decoder_x1_2_o1);
endmodule

module decoder_x3 (
  input  [2:0] i,
  output o0,
  output o1,
  output o2,
  output o3,
  output o4,
  output o5,
  output o6,
  output o7
);

  wire decoder_x1_1_o0, decoder_x1_1_o1, decoder_x2_1_o0, decoder_x2_1_o1, decoder_x2_1_o2, decoder_x2_1_o3;

  decoder_x2 decoder_x2_1 (
    .i(i[1:0]), .o0(decoder_x2_1_o0), .o1(decoder_x2_1_o1), .o2(decoder_x2_1_o2), .o3(decoder_x2_1_o3));
  decoder_x1 decoder_x1_1 (.i(i[2]), .o0(decoder_x1_1_o0), .o1(decoder_x1_1_o1));
  and and_1 (o0, decoder_x2_1_o0, decoder_x1_1_o0);
  and and_2 (o1, decoder_x2_1_o1, decoder_x1_1_o0);
  and and_3 (o2, decoder_x2_1_o2, decoder_x1_1_o0);
  and and_4 (o3, decoder_x2_1_o3, decoder_x1_1_o0);
  and and_5 (o4, decoder_x2_1_o0, decoder_x1_1_o1);
  and and_6 (o5, decoder_x2_1_o1, decoder_x1_1_o1);
  and and_7 (o6, decoder_x2_1_o2, decoder_x1_1_o1);
  and and_8 (o7, decoder_x2_1_o3, decoder_x1_1_o1);
endmodule

module decoder_x4 (
  input  [3:0] i,
  output d0,
  output d1,
  output d2,
  output d3,
  output d4,
  output d5,
  output d6,
  output d7,
  output d8,
  output d9,
  output d10,
  output d11,
  output d12,
  output d13,
  output d14,
  output d15
);

  wire decoder_x2_1_o0, decoder_x2_1_o1, decoder_x2_1_o2, decoder_x2_1_o3, decoder_x2_2_o0, decoder_x2_2_o1,
       decoder_x2_2_o2, decoder_x2_2_o3;

  decoder_x2 decoder_x2_1 (
    .i(i[1:0]), .o0(decoder_x2_1_o0), .o1(decoder_x2_1_o1), .o2(decoder_x2_1_o2), .o3(decoder_x2_1_o3));
  decoder_x2 decoder_x2_2 (
    .i(i[3:2]), .o0(decoder_x2_2_o0), .o1(decoder_x2_2_o1), .o2(decoder_x2_2_o2), .o3(decoder_x2_2_o3));
  and and_1 (d0, decoder_x2_1_o0, decoder_x2_2_o0);
  and and_2 (d1, decoder_x2_1_o1, decoder_x2_2_o0);
  and and_3 (d2, decoder_x2_1_o2, decoder_x2_2_o0);
  and and_4 (d3, decoder_x2_1_o3, decoder_x2_2_o0);
  and and_5 (d4, decoder_x2_1_o0, decoder_x2_2_o1);
  and and_6 (d5, decoder_x2_1_o1, decoder_x2_2_o1);
  and and_7 (d6, decoder_x2_1_o2, decoder_x2_2_o1);
  and and_8 (d7, decoder_x2_1_o3, decoder_x2_2_o1);
  and and_9 (d8, decoder_x2_1_o0, decoder_x2_2_o2);
  and and_10 (d9, decoder_x2_1_o1, decoder_x2_2_o2);
  and and_11 (d10, decoder_x2_1_o2, decoder_x2_2_o2);
  and and_12 (d11, decoder_x2_1_o3, decoder_x2_2_o2);
  and and_13 (d12, decoder_x2_1_o0, decoder_x2_2_o3);
  and and_14 (d13, decoder_x2_1_o1, decoder_x2_2_o3);
  and and_15 (d14, decoder_x2_1_o2, decoder_x2_2_o3);
  and and_16 (d15, decoder_x2_1_o3, decoder_x2_2_o3);
endmodule

module seg7_output (
  input  one,
  input  two,
  input  three,
  input  four,
  input  five,
  input  six,
  input  seven,
  input  eight,
  input  nine,
  input  zero,
  output a,
  output b,
  output c,
  output d,
  output e,
  output f,
  output g
);

  wire or_1_out, or_2_out, or_3_out, or_4_out, or_5_out, or_6_out, or_7_out, or_8_out, or_9_out, or_10_out,
       or_11_out, or_12_out, or_13_out, or_14_out, or_15_out, or_16_out, or_17_out, or_18_out, or_19_out,
       or_20_out, or_21_out, or_22_out, or_23_out, or_24_out, or_26_out, or_27_out, or_29_out, or_30_out,
       or_31_out, or_32_out, or_33_out, or_36_out, or_38_out, or_40_out;

  or or_1 (or_1_out, two, three);
  or or_2 (or_2_out, five, seven);
  or or_3 (or_3_out, eight, nine);
  or or_4 (or_4_out, zero, six);
  or or_5 (or_5_out, one, two);
  or or_6 (or_6_out, three, four);
  or or_7 (or_7_out, seven, eight);
  or or_8 (or_8_out, nine, zero);
  or or_9 (or_9_out, one, three);
  or or_10 (or_10_out, four, five);
  or or_11 (or_11_out, six, seven);
  or or_12 (or_12_out, eight, nine);
  or or_13 (or_13_out, two, three);
  or or_14 (or_14_out, five, six);
  or or_15 (or_15_out, eight, zero);
  or or_16 (or_16_out, two, six);
  or or_17 (or_17_out, eight, zero);
  or or_18 (or_18_out, four, five);
  or or_19 (or_19_out, six, eight);
  or or_20 (or_20_out, nine, zero);
  or or_21 (or_21_out, two, three);
  or or_22 (or_22_out, four, five);
  or or_23 (or_23_out, six, eight);
  or or_24 (or_24_out, or_1_out, or_2_out);
  or or_25 (a, or_24_out, or_26_out);
  or or_26 (or_26_out, or_3_out, or_4_out);
  or or_27 (or_27_out, or_5_out, or_6_out);
  or or_28 (b, or_27_out, or_29_out);
  or or_29 (or_29_out, or_7_out, or_8_out);
  or or_30 (or_30_out, or_9_out, or_10_out);
  or or_31 (or_31_out, or_30_out, or_32_out);
  or or_32 (or_32_out, or_11_out, or_12_out);
  or or_33 (or_33_out, or_13_out, or_14_out);
  or or_34 (d, or_33_out, or_15_out);
  or or_35 (e, or_16_out, or_17_out);
  or or_36 (or_36_out, or_18_out, or_19_out);
  or or_37 (f, or_36_out, or_20_out);
  or or_38 (or_38_out, or_21_out, or_22_out);
  or or_39 (g, or_38_out, or_40_out);
  or or_40 (or_40_out, or_23_out, nine);
  or or_41 (c, or_31_out, zero);

  // Notes on the sheet:
  //   Segment  A
  //   Segment  C
  //   Segment  D
  //   Segment  E
  //   Segment  F
  //   Segment  G
  //   Segment  B
endmodule

module seg7_with_decoder (
  input  [3:0] i
);

  wire decoder_x4_1_d0, decoder_x4_1_d1, decoder_x4_1_d2, decoder_x4_1_d3, decoder_x4_1_d4, decoder_x4_1_d5,
       decoder_x4_1_d6, decoder_x4_1_d7, decoder_x4_1_d8, decoder_x4_1_d9, seg7_output_1_a, seg7_output_1_b,
       seg7_output_1_c, seg7_output_1_d, seg7_output_1_e, seg7_output_1_f, seg7_output_1_g;

  decoder_x4 decoder_x4_1 (
    .i(i), .d0(decoder_x4_1_d0), .d1(decoder_x4_1_d1), .d2(decoder_x4_1_d2), .d3(decoder_x4_1_d3),
    .d4(decoder_x4_1_d4), .d5(decoder_x4_1_d5), .d6(decoder_x4_1_d6), .d7(decoder_x4_1_d7),
    .d8(decoder_x4_1_d8), .d9(decoder_x4_1_d9));  // open: d10, d11, d12, d13, d14, d15
  seg7_output seg7_output_1 (
    .one(decoder_x4_1_d1), .two(decoder_x4_1_d2), .three(decoder_x4_1_d3), .four(decoder_x4_1_d4),
    .five(decoder_x4_1_d5), .six(decoder_x4_1_d6), .seven(decoder_x4_1_d7), .eight(decoder_x4_1_d8),
    .nine(decoder_x4_1_d9), .zero(decoder_x4_1_d0), .a(seg7_output_1_a), .b(seg7_output_1_b),
    .c(seg7_output_1_c), .d(seg7_output_1_d), .e(seg7_output_1_e), .f(seg7_output_1_f), .g(seg7_output_1_g));
  _7_Segment_Display #(.decimalPoint("false")) u_7_segment_display_1 (
    .g(seg7_output_1_g), .f(seg7_output_1_f), .a(seg7_output_1_a), .b(seg7_output_1_b), .e(seg7_output_1_e),
    .d(seg7_output_1_d), .c(seg7_output_1_c));
endmodule

module seg7_optimized (
  input  one,
  input  two,
  input  three,
  input  four,
  input  five,
  input  six,
  input  seven,
  input  eight,
  input  nine,
  input  zero
);

  wire nand_1_out, nand_2_out, nand_3_out, nand_4_out, nor_1_out, nor_2_out, nor_3_out, nor_4_out, nor_5_out,
       nor_6_out, nor_7_out, or_1_out, or_2_out, or_3_out, or_4_out, or_5_out, or_6_out, or_7_out, or_8_out,
       or_9_out, or_10_out;

  nor nor_1 (nor_1_out, one, three);
  nor nor_2 (nor_2_out, three, two);
  or or_1 (or_1_out, four, one);
  or or_2 (or_2_out, five, four);
  nor nor_3 (nor_3_out, six, two);
  or or_3 (or_3_out, five, three);
  nor nor_4 (nor_4_out, eight, zero);
  nor nor_5 (nor_5_out, nine, eight);
  or or_4 (or_4_out, zero, seven);
  or or_5 (or_5_out, or_2_out, six);
  nand nand_1 (nand_1_out, nor_3_out, nor_4_out);
  nand nand_2 (nand_2_out, nor_2_out, nor_5_out);
  nor nor_6 (nor_6_out, or_5_out, zero);
  or or_6 (or_6_out, or_3_out, nand_1_out);
  or or_7 (or_7_out, nand_2_out, or_5_out);
  or or_8 (or_8_out, nand_2_out, or_4_out);
  or or_9 (or_9_out, or_8_out, or_1_out);
  nand nand_3 (nand_3_out, nor_5_out, nor_6_out);
  or or_10 (or_10_out, or_8_out, five);
  nor nor_7 (nor_7_out, nand_3_out, seven);
  nand nand_4 (nand_4_out, nor_1_out, nor_7_out);
  _7_Segment_Display #(.decimalPoint("false")) u_7_segment_display_1 (
    .g(or_7_out), .f(nand_3_out), .a(or_10_out), .b(or_9_out), .e(nand_1_out), .d(or_6_out), .c(nand_4_out));
endmodule
