// Logisim project latchesAndFlipFlops.circ as structural Verilog: 16 circuits, main circuit sr_nor_latch
module sr_nor_latch (
  input  R,
  input  S,
  output Q,
  output notQ
);

  nor nor_1 (Q, R, notQ);
  nor nor_2 (notQ, Q, S);
endmodule

module sr_nand_latch (
  input  notS,
  input  notR,
  output Q,
  output notQ
);

  nand nand_1 (Q, notS, notQ);
  nand nand_2 (notQ, Q, notR);
endmodule

module sr_or_latch (
  input  S,
  input  R,
  output Q
);

  wire not_1_out, or_1_out;

  or or_1 (or_1_out, Q, S);
  not not_1 (not_1_out, R);
  and and_1 (Q, or_1_out, not_1_out);
endmodule

module gated_sr_latch (
  input  R,
  input  E,
  input  S,
  output Q,
  output notQ
);

  wire and_1_out, and_2_out;

  and and_1 (and_1_out, R, E);
  and and_2 (and_2_out, E, S);
  nor nor_1 (Q, and_1_out, notQ);
  nor nor_2 (notQ, Q, and_2_out);
endmodule

module d_latch (
  input  D,
  output Q,
  output notQ
);

  wire not_1_out;

  not not_1 (not_1_out, D);
  nand nand_1 (Q, D, notQ);
  nand nand_2 (notQ, Q, not_1_out);
endmodule

module gated_d_latch (
  input  D,
  input  E,
  output Q,
  output notQ
);

  wire nand_1_out, nand_2_out, not_1_out;

  not not_1 (not_1_out, D);
  nand nand_1 (nand_1_out, D, E);
  nand nand_2 (nand_2_out, E, not_1_out);
  nand nand_3 (Q, nand_1_out, notQ);
  nand nand_4 (notQ, Q, nand_2_out);
endmodule

module earle_latch (
  input  E,
  input  D,
  output Q
);

  wire nand_1_out, nand_2_out, nand_3_out, not_1_out;

  not not_1 (not_1_out, E);
  nand nand_1 (nand_1_out, E, D);
  nand nand_2 (nand_2_out, D, Q);
  nand nand_3 (nand_3_out, Q, not_1_out);
  nand nand_4 (Q, nand_1_out, nand_2_out, nand_3_out);
endmodule

module d_flip_flop (
  input  Clk,
  input  D,
  output Q,
  output notQ
);

  wire nand_1_out, nand_2_out, nand_3_out, nand_4_out;

  nand nand_1 (nand_1_out, nand_4_out, nand_2_out);
  nand nand_2 (nand_2_out, nand_1_out, Clk);
  nand nand_3 (nand_3_out, nand_2_out, Clk, nand_4_out);
  nand nand_4 (nand_4_out, nand_3_out, D);
  nand nand_5 (Q, nand_2_out, notQ);
  nand nand_6 (notQ, Q, nand_3_out);
endmodule

module d_sr_flip_flop (
  input  notS,
  input  Clk,
  input  D,
  input  notR,
  output Q,
  output notQ
);

  wire nand_1_out, nand_2_out, nand_3_out, nand_4_out;

  nand nand_1 (nand_1_out, notS, nand_4_out, nand_2_out);
  nand nand_2 (nand_2_out, nand_1_out, Clk, notR);
  nand nand_3 (nand_3_out, nand_2_out, Clk, nand_4_out);
  nand nand_4 (nand_4_out, nand_3_out, D, notR);
  nand nand_5 (Q, notS, nand_2_out, notQ);
  nand nand_6 (notQ, Q, nand_3_out, notR);

  // Notes on the sheet:
  //   The mixing of the SR latch function in to the d flip flop here gives us something that will be useful later
  //   But it allows us to force the circut to initalize in to a valid starting state using combinational logic rather than sequential
endmodule

module master_slave_d_flip_flop (
  input  D,
  input  Clk,
  output Q,
  output notQ
);

  wire gated_d_latch_1_q, not_1_out;

  gated_d_latch gated_d_latch_1 (.D(D), .E(Clk), .Q(gated_d_latch_1_q));  // open: notQ
  not not_1 (not_1_out, Clk);
  gated_d_latch gated_d_latch_2 (.D(gated_d_latch_1_q), .E(not_1_out), .Q(Q), .notQ(notQ));
endmodule

module dual_edge_d_flip_flop (
  input  Clk,
  input  D,
  output Q
);

  wire d_flip_flop_1_q, d_flip_flop_2_q, not_1_out;

  not not_1 (not_1_out, Clk);
  d_flip_flop d_flip_flop_1 (.Clk(not_1_out), .D(D), .Q(d_flip_flop_1_q));  // open: notQ
  d_flip_flop d_flip_flop_2 (.Clk(Clk), .D(D), .Q(d_flip_flop_2_q));  // open: notQ
  Multiplexer multiplexer_1 (.in0(d_flip_flop_1_q), .in1(d_flip_flop_2_q), .out(Q));  // open: sel

  // Notes on the sheet:
  //   You will notice logism doesnt like this it initializes in to an invalid state
  //   Once the clock pulses one it stablizes but that inital state is invalid
endmodule

module dual_edge_d_sr_flip_flop (
  input  Clk,
  input  D,
  input  in_3,
  input  in_4,
  output Q
);

  wire d_sr_flip_flop_1_q, d_sr_flip_flop_2_q, not_1_out;

  not not_1 (not_1_out, Clk);
  d_sr_flip_flop d_sr_flip_flop_1 (
    .notS(in_3), .Clk(not_1_out), .D(D), .notR(in_4), .Q(d_sr_flip_flop_1_q));  // open: notQ
  d_sr_flip_flop d_sr_flip_flop_2 (.notS(in_3), .Clk(Clk), .D(D), .notR(in_4), .Q(d_sr_flip_flop_2_q));  // open: notQ
  Multiplexer multiplexer_1 (.in0(d_sr_flip_flop_1_q), .in1(d_sr_flip_flop_2_q), .out(Q));  // open: sel

  // Notes on the sheet:
  //   in_4: initial=0x1
  //   Either on or off depending on if S or R is set
  //   Using our D SR flip flop we can use the the SR inputs to initalize into a valid state
endmodule

module t_flip_flop (
  input  in_1,
  input  Clk,
  input  T,
  input  in_4,
  output Q
);

  wire xor_1_out;

  xor xor_1 (xor_1_out, T, Q);
  d_sr_flip_flop d_sr_flip_flop_1 (.notS(in_1), .Clk(Clk), .D(xor_1_out), .notR(in_4), .Q(Q));  // open: notQ

  // Notes on the sheet:
  //   in_1: initial=0x1
  //   Same deal here we use S and R to init the flip flop
endmodule

module jk_flip_flop (
  input  J,
  input  Clk,
  input  K,
  input  E,
  output Q,
  output notQ
);

  wire and_1_out, nand_1_out, nand_2_out;

  nand nand_1 (nand_1_out, notQ, J, Clk);
  nand nand_2 (nand_2_out, Clk, K, Q);
  and and_1 (and_1_out, nand_2_out, E);
  sr_nand_latch sr_nand_latch_1 (.notS(nand_1_out), .notR(and_1_out), .Q(Q), .notQ(notQ));

  // Notes on the sheet:
  //   It also does work as an enable pin
  //   The reason is that the state of this flip flop is subject to a race condition
  //   While not strictly part of the formal design for a JK flip flop
  //   Not that this does not work in logism although it is simpliest layout for a jk flip flop
  //   In the real world (or a simulator with proper gate delay) we can resolve the race condition 
  //   by deliberately making one path take longer allowing the circut to settting in to a stable state
  //   This is needed because logism doesnt allow to set output initial pin value
  //   So the simulation starts in error. Starting with this off allows the circut to initialize in a valid state
endmodule

module ms_jk_flip_flop (
  input  J,
  input  Clk,
  input  K,
  input  E,
  output Q,
  output notQ
);

  wire and_1_out, nand_1_out, nand_2_out, nand_3_out, nand_4_out, not_1_out, sr_nand_latch_1_notq,
       sr_nand_latch_1_q;

  nand nand_1 (nand_1_out, notQ, J, Clk);
  nand nand_2 (nand_2_out, Clk, K, Q);
  and and_1 (and_1_out, nand_2_out, E);
  sr_nand_latch sr_nand_latch_1 (
    .notS(nand_1_out), .notR(and_1_out), .Q(sr_nand_latch_1_q), .notQ(sr_nand_latch_1_notq));
  not not_1 (not_1_out, Clk);
  nand nand_3 (nand_3_out, not_1_out, sr_nand_latch_1_q);
  nand nand_4 (nand_4_out, sr_nand_latch_1_notq, not_1_out);
  sr_nand_latch sr_nand_latch_2 (.notS(nand_3_out), .notR(nand_4_out), .Q(Q), .notQ(notQ));

  // Notes on the sheet:
  //   the second half updates the second latch
  //   we can use a master slave setup with two sr latches to resolve the race condition
  //   the first latch updates on one half of the clock signal and then holds
  //   if you trace the wires you can see that neither latch is ever in an unstable state
endmodule

module d_from_jk (
  input  D,
  input  Clk,
  input  E,
  output Q,
  output notQ
);

  wire not_1_out;

  not not_1 (not_1_out, D);
  ms_jk_flip_flop ms_jk_flip_flop_1 (.J(D), .Clk(Clk), .K(not_1_out), .E(E), .Q(Q), .notQ(notQ));

  // Notes on the sheet:
  //   The JK flip flop can be used to make all other types of flip flops
endmodule
