// Logisim project mipsALU.circ as structural Verilog: 32 circuits, main circuit v1_fullAdder
module v1_fullAdder (
  input  A,
  input  B,
  input  Cin,
  output Cout,
  output O
);

  wire and_1_out, and_2_out, xor_1_out;

  and and_1 (and_1_out, A, B);
  xor xor_1 (xor_1_out, A, B);
  and and_2 (and_2_out, xor_1_out, Cin);
  or or_1 (Cout, and_1_out, and_2_out);
  xor xor_2 (O, xor_1_out, Cin);
endmodule

module v1_alu (
  input  op1,
  input  op0,
  input  A,
  input  B,
  input  Cin,
  output Cout,
  output O,
  output out_8
);

  wire and_1_out, nor_1_out, or_1_out, v1_fulladder_1_cout, v1_fulladder_1_o, xor_1_out;

  v1_fullAdder v1_fulladder_1 (.A(A), .B(B), .Cin(Cin), .Cout(v1_fulladder_1_cout), .O(v1_fulladder_1_o));
  and and_1 (and_1_out, A, B);
  or or_1 (or_1_out, A, B);
  xor xor_1 (xor_1_out, A, B);
  nor nor_1 (nor_1_out, op0, op1);
  and and_2 (Cout, nor_1_out, v1_fulladder_1_cout);
  mux4_1 mux4_1_1 (.A(v1_fulladder_1_o), .B(and_1_out), .C(or_1_out), .D(xor_1_out), .s0(op0), .s1(op1), .O(O));
  not not_1 (out_8, O);

  // Notes on the sheet:
  //   1bit ALU
  //   4 functions
  //   add op: 00
  //   and op:01
  //   or op: 10
  //   xor op:11
  //   Flags
  //   Z: Zero: Is output 0
  //   C: Carry: Carry out of arithmetic, 0 always on logic
endmodule

module v1a_fullAdder (
  input  A,
  input  B,
  input  Cin,
  output AndB,
  output AorB,
  output AxorB,
  output Cout,
  output O
);

  wire and_2_out;

  and and_1 (AndB, A, B);
  xor xor_1 (AxorB, A, B);
  or or_1 (AorB, AndB, AxorB);
  and and_2 (and_2_out, AxorB, Cin);
  or or_2 (Cout, AndB, and_2_out);
  xor xor_2 (O, AxorB, Cin);

  // Notes on the sheet:
  //   We can hijack some of the work our gates do in the full adder to reduce gate count
endmodule

module v1a_alu (
  input  op1,
  input  op0,
  input  A,
  input  B,
  input  Cin,
  output Cout,
  output O,
  output Z
);

  wire nor_1_out, v1a_fulladder_1_andb, v1a_fulladder_1_aorb, v1a_fulladder_1_axorb, v1a_fulladder_1_cout,
       v1a_fulladder_1_o;

  v1a_fullAdder v1a_fulladder_1 (
    .A(A), .B(B), .Cin(Cin), .AndB(v1a_fulladder_1_andb), .AorB(v1a_fulladder_1_aorb),
    .AxorB(v1a_fulladder_1_axorb), .Cout(v1a_fulladder_1_cout), .O(v1a_fulladder_1_o));
  nor nor_1 (nor_1_out, op0, op1);
  and and_1 (Cout, nor_1_out, v1a_fulladder_1_cout);
  mux4_1 mux4_1_1 (
    .A(v1a_fulladder_1_o), .B(v1a_fulladder_1_andb), .C(v1a_fulladder_1_aorb), .D(v1a_fulladder_1_axorb),
    .s0(op0), .s1(op1), .O(O));
  not not_1 (Z, O);

  // Notes on the sheet:
  //   1bit ALU
  //   4 functions
  //   add op: 00
  //   and op:01
  //   or op: 10
  //   xor op:11
  //   Flags
  //   Z: Zero: Is output 0
  //   C: Carry: Carry out of arithmetic, 0 always on logic
endmodule

module v2_alu (
  input  [2:0] funct,
  input  \logic ,
  input  A,
  input  B,
  input  InvertB,
  input  Cin,
  output O,
  output Z,
  output less,
  output V,
  output prevCin,
  output Cout,
  output uless
);

  wire not_1_out, v1a_fulladder_1_andb, v1a_fulladder_1_aorb, v1a_fulladder_1_axorb, v1a_fulladder_1_cout,
       v1a_fulladder_1_o, xor_1_out, xor_2_out;

  xor xor_1 (xor_1_out, B, InvertB);
  v1a_fullAdder v1a_fulladder_1 (
    .A(A), .B(xor_1_out), .Cin(Cin), .AndB(v1a_fulladder_1_andb), .AorB(v1a_fulladder_1_aorb),
    .AxorB(v1a_fulladder_1_axorb), .Cout(v1a_fulladder_1_cout), .O(v1a_fulladder_1_o));
  xor xor_2 (xor_2_out, v1a_fulladder_1_cout, Cin);
  not not_1 (not_1_out, v1a_fulladder_1_aorb);
  xor xor_3 (less, v1a_fulladder_1_o, xor_2_out);
  not not_2 (uless, v1a_fulladder_1_cout);
  Multiplexer #(.select(3)) multiplexer_1 (
    .in0(v1a_fulladder_1_o), .in1(1'b0), .in2(v1a_fulladder_1_o), .in3(1'b0), .in4(v1a_fulladder_1_andb),
    .in5(v1a_fulladder_1_aorb), .in6(v1a_fulladder_1_axorb), .in7(not_1_out), .out(O));  // open: sel
  xor xor_4 (V, xor_2_out, \logic );
  xor xor_5 (Cout, \logic , v1a_fulladder_1_cout);
  not not_3 (Z, O);

  assign prevCin = Cin;

  // Notes on the sheet:
  //   001 and
  //   010 or
  //   011 xor
  //   100 nor
  //   Flags
  //   1bit ALU
  //   5 functions
  //   000 add/sub
  //   Control Signals
  //   InvertB : invert input B
  //   Cin: Set Carry in
  //   logic: is logic opperation
  //   Z: Zero: 1 if output is 0
  //   less: signed a < b
  //   uless: unsigned a < b
  //   Cout: Carry: Carry out of arithmetic, 0 always on logic
  //   V: Overflow: Is signed output overflowed, 0 always on logic
  //   000/010 add/sub
  //   100 and
  //   101 or
  //   110 xor
  //   111 nor
  //   Note all logic functions start with 1, this makes for a useful detection
  //   However I am going to leave the logic pin explicit for now; all control signals will eventually be handled
endmodule

module x2_alu (
  input  \logic ,
  input  InvertB,
  input  Cin,
  input  [2:0] funct,
  input  [1:0] A,
  input  [1:0] B,
  output [1:0] O,
  output Z,
  output uless,
  output Cout,
  output V,
  output less,
  output prevCin
);

  wire v2_alu_1_cout, v2_alu_1_z, v2_alu_2_z;

  v2_alu v2_alu_1 (
    .funct(funct), .\logic (\logic ), .A(A[0]), .B(B[0]), .InvertB(InvertB), .Cin(Cin), .O(O[0]),
    .Z(v2_alu_1_z), .Cout(v2_alu_1_cout));  // open: less, V, prevCin, uless
  v2_alu v2_alu_2 (
    .funct(funct), .\logic (\logic ), .A(A[1]), .B(B[1]), .InvertB(InvertB), .Cin(v2_alu_1_cout), .O(O[1]),
    .Z(v2_alu_2_z), .prevCin(prevCin), .Cout(Cout));  // open: less, V, uless
  xor xor_1 (V, Cout, prevCin);
  and and_1 (Z, v2_alu_1_z, v2_alu_2_z);
  not not_1 (uless, Cout);
  xor xor_2 (less, V, O[1]);
endmodule

module x4_alu (
  input  \logic ,
  input  InvertB,
  input  Cin,
  input  [2:0] funct,
  input  [3:0] A,
  input  [3:0] B,
  output [3:0] O,
  output Z,
  output uless,
  output Cout,
  output V,
  output less,
  output prevCin
);

  wire x2_alu_1_cout, x2_alu_1_z, x2_alu_2_z;

  x2_alu x2_alu_1 (
    .\logic (\logic ), .InvertB(InvertB), .Cin(Cin), .funct(funct), .A(A[1:0]), .B(B[1:0]), .O(O[1:0]),
    .Z(x2_alu_1_z), .Cout(x2_alu_1_cout));  // open: uless, V, less, prevCin
  x2_alu x2_alu_2 (
    .\logic (\logic ), .InvertB(InvertB), .Cin(x2_alu_1_cout), .funct(funct), .A(A[3:2]), .B(B[3:2]),
    .O(O[3:2]), .Z(x2_alu_2_z), .Cout(Cout), .prevCin(prevCin));  // open: uless, V, less
  xor xor_1 (V, Cout, prevCin);
  and and_1 (Z, x2_alu_1_z, x2_alu_2_z);
  not not_1 (uless, Cout);
  xor xor_2 (less, V, O[3]);
endmodule

module x8_alu (
  input  \logic ,
  input  InvertB,
  input  Cin,
  input  [2:0] funct,
  input  [7:0] A,
  input  [7:0] B,
  output [7:0] O,
  output Z,
  output uless,
  output Cout,
  output V,
  output less,
  output prevCin
);

  wire x4_alu_1_cout, x4_alu_1_z, x4_alu_2_z;

  x4_alu x4_alu_1 (
    .\logic (\logic ), .InvertB(InvertB), .Cin(Cin), .funct(funct), .A(A[3:0]), .B(B[3:0]), .O(O[3:0]),
    .Z(x4_alu_1_z), .Cout(x4_alu_1_cout));  // open: uless, V, less, prevCin
  x4_alu x4_alu_2 (
    .\logic (\logic ), .InvertB(InvertB), .Cin(x4_alu_1_cout), .funct(funct), .A(A[7:4]), .B(B[7:4]),
    .O(O[7:4]), .Z(x4_alu_2_z), .Cout(Cout), .prevCin(prevCin));  // open: uless, V, less
  xor xor_1 (V, Cout, prevCin);
  and and_1 (Z, x4_alu_1_z, x4_alu_2_z);
  not not_1 (uless, Cout);
  xor xor_2 (less, V, O[7]);
endmodule

module x16_alu (
  input  \logic ,
  input  InvertB,
  input  Cin,
  input  [2:0] funct,
  input  [15:0] A,
  input  [15:0] B,
  output [15:0] O,
  output Z,
  output uless,
  output Cout,
  output V,
  output less,
  output prevCin
);

  wire x8_alu_1_cout, x8_alu_1_z, x8_alu_2_z;

  x8_alu x8_alu_1 (
    .\logic (\logic ), .InvertB(InvertB), .Cin(Cin), .funct(funct), .A(A[7:0]), .B(B[7:0]), .O(O[7:0]),
    .Z(x8_alu_1_z), .Cout(x8_alu_1_cout));  // open: uless, V, less, prevCin
  x8_alu x8_alu_2 (
    .\logic (\logic ), .InvertB(InvertB), .Cin(x8_alu_1_cout), .funct(funct), .A(A[15:8]), .B(B[15:8]),
    .O(O[15:8]), .Z(x8_alu_2_z), .Cout(Cout), .prevCin(prevCin));  // open: uless, V, less
  xor xor_1 (V, Cout, prevCin);
  and and_1 (Z, x8_alu_1_z, x8_alu_2_z);
  not not_1 (uless, Cout);
  xor xor_2 (less, V, O[15]);
endmodule

module x32_alu (
  input  \logic ,
  input  InvertB,
  input  Cin,
  input  [2:0] funct,
  input  [31:0] A,
  input  [31:0] B,
  output [31:0] O,
  output Z,
  output uless,
  output Cout,
  output V,
  output less,
  output prevCin
);

  wire x16_alu_1_cout, x16_alu_1_z, x16_alu_2_z;

  x16_alu x16_alu_1 (
    .\logic (\logic ), .InvertB(InvertB), .Cin(Cin), .funct(funct), .A(A[15:0]), .B(B[15:0]), .O(O[15:0]),
    .Z(x16_alu_1_z), .Cout(x16_alu_1_cout));  // open: uless, V, less, prevCin
  x16_alu x16_alu_2 (
    .\logic (\logic ), .InvertB(InvertB), .Cin(x16_alu_1_cout), .funct(funct), .A(A[31:16]), .B(B[31:16]),
    .O(O[31:16]), .Z(x16_alu_2_z), .Cout(Cout), .prevCin(prevCin));  // open: uless, V, less
  xor xor_1 (V, Cout, prevCin);
  and and_1 (Z, x16_alu_1_z, x16_alu_2_z);
  not not_1 (uless, Cout);
  xor xor_2 (less, V, O[31]);

  // Notes on the sheet:
  //   100 and
  //   101 or
  //   110 xor
  //   111 nor
  //   Flags
  //   32bit ALU
  //   5 functions
  //   000/010 add/sub
  //   Control Signals
  //   InvertB : invert input B
  //   Cin: Set Carry in
  //   logic: is logic opperation
  //   Z: Zero: 1 if output is 0
  //   less: signed a < b
  //   uless: unsigned a < b
  //   Cout: Carry: Carry out of arithmetic, 0 always on logic
  //   V: Overflow: Is signed output overflowed, 0 always on logic
endmodule

module x32_alu_with_shift (
  input  \logic ,
  input  InvertB,
  input  Cin,
  input  [2:0] funct,
  input  [31:0] A,
  input  [31:0] B,
  output [31:0] O,
  output Z,
  output uless,
  output Cout,
  output V,
  output less,
  output [31:0] Lshift,
  output [31:0] Rshift,
  output [31:0] ArithShift
);

  x32_alu x32_alu_1 (
    .\logic (\logic ), .InvertB(InvertB), .Cin(Cin), .funct(funct), .A(A), .B(B), .O(O), .Z(Z),
    .uless(uless), .Cout(Cout), .V(V), .less(less));  // open: prevCin
  Shifter #(.width(32)) shifter_1 (.in(A), .\dist (B[4:0]), .out(Lshift));
  Shifter #(.shift("lr"), .width(32)) shifter_2 (.in(A), .\dist (B[4:0]), .out(Rshift));
  Shifter #(.shift("ar"), .width(32)) shifter_3 (.in(A), .\dist (B[4:0]), .out(ArithShift));

  // Notes on the sheet:
  //   Note while we manually built a RL shifter with arithmatic functionality
  //   logism itself can get pretty laggy nesting all those sub circuts
  //   so for the sake of performace we will place 3 of the built-in shifters here and select between the outputs
endmodule

module x32_alu_complete (
  input  \logic ,
  input  InvertB,
  input  Cin,
  input  [2:0] funct,
  input  [31:0] A,
  input  [31:0] shamt,
  input  [31:0] B,
  input  srl_sra,
  input  sll_srl,
  input  slt_sltu,
  input  O_slt,
  input  shift_O,
  output Z,
  output [31:0] O,
  output C,
  output V
);

  wire x32_alu_with_shift_1_less, x32_alu_with_shift_1_uless;
  wire [0:0] multiplexer_3_out;
  wire [31:0] multiplexer_1_out, multiplexer_2_out, multiplexer_4_out, x32_alu_with_shift_1_arithshift,
       x32_alu_with_shift_1_lshift, x32_alu_with_shift_1_o, x32_alu_with_shift_1_rshift;

  Multiplexer #(.width(32)) multiplexer_1 (.in0(shamt), .in1(B), .out(multiplexer_1_out), .sel(shift_O));
  x32_alu_with_shift x32_alu_with_shift_1 (
    .\logic (\logic ), .InvertB(InvertB), .Cin(Cin), .funct(funct), .A(A), .B(multiplexer_1_out),
    .O(x32_alu_with_shift_1_o), .Z(Z), .uless(x32_alu_with_shift_1_uless), .Cout(C), .V(V),
    .less(x32_alu_with_shift_1_less), .Lshift(x32_alu_with_shift_1_lshift),
    .Rshift(x32_alu_with_shift_1_rshift), .ArithShift(x32_alu_with_shift_1_arithshift));
  Multiplexer #(.width(32)) multiplexer_2 (
    .in0(x32_alu_with_shift_1_rshift), .in1(x32_alu_with_shift_1_arithshift), .out(multiplexer_2_out),
    .sel(srl_sra));
  Multiplexer multiplexer_3 (
    .in0(x32_alu_with_shift_1_less), .in1(x32_alu_with_shift_1_uless), .out(multiplexer_3_out[0]),
    .sel(slt_sltu));
  Multiplexer #(.width(32)) multiplexer_4 (
    .in0(x32_alu_with_shift_1_lshift), .in1(multiplexer_2_out), .out(multiplexer_4_out), .sel(sll_srl));
  Multiplexer #(.select(2), .width(32)) multiplexer_5 (
    .in0(multiplexer_4_out), .in1(x32_alu_with_shift_1_o), .in2({32{1'b0}}),
    .in3({{31{1'b0}}, multiplexer_3_out[0]}), .out(O), .sel({O_slt, shift_O}));

  // Notes on the sheet:
  //   jr/jalr
  //   funct codes
  //   Flags Z V C will be output
  //   Unimplimented instructions
  //   addu/subu
  //   ssl 00 00 00
  //   srl 00 00 10
  //   sra 00 00 11
  //   add 10 00 00
  //   sub 10 00 10
  //   and 10 01 00
  //   or 10 01 01
  //   xor 10 01 10
  //   nor 10 01 11
  //   slt 10 10 10
  //   sltu 10 10 11
  //   Here we shall wrap everything together
  //   It is undefined for shift, and less than
  //   mult/div and asociated register functions
  //   All function outputs will be mux'd and output on one pin
  //   Note Z is only defined for logic and arthmetic functions
  //   All control signals will be derived from standard mips funct codes
  //   This is fine because we only use Z for the equality test for beq which sets the same control as sub
  //   The messy cross over could be resolved with the addition of a few not's but eh
endmodule

module alu_controller (
  input  [5:0] funct,
  input  [4:0] shamt,
  output \logic ,
  output InvertB_Cin,
  output [2:0] functOut,
  output srl_sra,
  output slt_sltu,
  output sll_srl,
  output O_slt,
  output shift_O,
  output [31:0] extendedShamt
);

  wire not_1_out;

  not not_1 (not_1_out, funct[2]);
  and and_1 (InvertB_Cin, not_1_out, funct[1]);

  assign extendedShamt = {{27{1'b0}}, shamt};
  assign functOut = funct[2:0];
  assign \logic  = funct[2];
  assign O_slt = funct[3];
  assign shift_O = funct[5];
  assign sll_srl = funct[1];
  assign slt_sltu = funct[0];
  assign srl_sra = funct[0];

  // Notes on the sheet:
  //   alu_controller decodes funct and outputs control signals to alu
  //   also takes shamt extends it to 32 bit so it can be passed to alu as input B
endmodule

module alu_and_controller (
  input  [5:0] funt,
  input  [4:0] shamt,
  input  [31:0] A,
  input  [31:0] B,
  output [31:0] O,
  output Z,
  output C,
  output V
);

  wire alu_controller_1_invertb_cin, alu_controller_1_logic, alu_controller_1_o_slt,
       alu_controller_1_shift_o, alu_controller_1_sll_srl, alu_controller_1_slt_sltu,
       alu_controller_1_srl_sra;
  wire [2:0] alu_controller_1_functout;
  wire [31:0] alu_controller_1_extendedshamt;

  alu_controller alu_controller_1 (
    .funct(funt), .shamt(shamt), .\logic (alu_controller_1_logic),
    .InvertB_Cin(alu_controller_1_invertb_cin), .functOut(alu_controller_1_functout),
    .srl_sra(alu_controller_1_srl_sra), .slt_sltu(alu_controller_1_slt_sltu),
    .sll_srl(alu_controller_1_sll_srl), .O_slt(alu_controller_1_o_slt), .shift_O(alu_controller_1_shift_o),
    .extendedShamt(alu_controller_1_extendedshamt));
  x32_alu_complete x32_alu_complete_1 (
    .srl_sra(alu_controller_1_srl_sra), .sll_srl(alu_controller_1_sll_srl),
    .slt_sltu(alu_controller_1_slt_sltu), .O_slt(alu_controller_1_o_slt), .shift_O(alu_controller_1_shift_o),
    .shamt(alu_controller_1_extendedshamt), .B(B), .\logic (alu_controller_1_logic),
    .InvertB(alu_controller_1_invertb_cin), .Cin(alu_controller_1_invertb_cin),
    .funct(alu_controller_1_functout), .A(A), .Z(Z), .C(C), .V(V), .O(O));

  // Notes on the sheet:
  //   And A and B from reg read
  //   We have finally packaged everything together
  //   We just need to pass the shamt and funct from the instruction
endmodule

module mux2_1 (
  input  A,
  input  B,
  input  S,
  output O
);

  wire and_1_out, and_2_out, not_1_out;

  not not_1 (not_1_out, S);
  and and_1 (and_1_out, B, S);
  or or_1 (O, and_1_out, and_2_out);
  and and_2 (and_2_out, A, not_1_out);
endmodule

module mux4_1 (
  input  A,
  input  B,
  input  C,
  input  D,
  input  s0,
  input  s1,
  output O
);

  wire mux2_1_1_o, mux2_1_2_o;

  mux2_1 mux2_1_1 (.A(A), .B(B), .S(s0), .O(mux2_1_1_o));
  mux2_1 mux2_1_2 (.A(C), .B(D), .S(s0), .O(mux2_1_2_o));
  mux2_1 mux2_1_3 (.A(mux2_1_1_o), .B(mux2_1_2_o), .S(s1), .O(O));
endmodule

module mux16_1 (
  input  s0,
  input  s1,
  input  s2,
  input  s3,
  input  i0,
  input  i1,
  input  i2,
  input  i3,
  input  i4,
  input  i5,
  input  i6,
  input  i7,
  input  i8,
  input  i9,
  input  i10,
  input  i11,
  input  i12,
  input  i13,
  input  i14,
  input  i15,
  output O
);

  wire mux4_1_1_o, mux4_1_2_o, mux4_1_3_o, mux4_1_4_o;

  mux4_1 mux4_1_1 (.A(i0), .B(i1), .C(i2), .D(i3), .s0(s0), .s1(s1), .O(mux4_1_1_o));
  mux4_1 mux4_1_2 (.A(i4), .B(i5), .C(i6), .D(i7), .s0(s0), .s1(s1), .O(mux4_1_2_o));
  mux4_1 mux4_1_3 (.A(i8), .B(i9), .C(i10), .D(i11), .s0(s0), .s1(s1), .O(mux4_1_3_o));
  mux4_1 mux4_1_4 (.A(i12), .B(i13), .C(i14), .D(i15), .s0(s0), .s1(s1), .O(mux4_1_4_o));
  mux4_1 mux4_1_5 (.A(mux4_1_1_o), .B(mux4_1_2_o), .C(mux4_1_3_o), .D(mux4_1_4_o), .s0(s2), .s1(s3), .O(O));
endmodule

module x1x1_Lshifter (
  input  A,
  input  ShiftIn,
  input  shift,
  output O
);

  mux2_1 mux2_1_1 (.A(A), .B(ShiftIn), .S(shift), .O(O));

  // Notes on the sheet:
  //   Note a 1bit shifter is midly pointless
endmodule

module x2x1_Lshifter (
  input  ShiftIn,
  input  [1:0] A,
  input  shift,
  output [1:0] O
);

  x1x1_Lshifter x1x1_lshifter_1 (.A(A[0]), .ShiftIn(ShiftIn), .shift(shift), .O(O[0]));
  x1x1_Lshifter x1x1_lshifter_2 (.A(A[1]), .ShiftIn(A[0]), .shift(shift), .O(O[1]));
endmodule

module x4x1_Lshifter (
  input  ShiftIn,
  input  [3:0] A,
  input  shift,
  output [3:0] O
);

  x2x1_Lshifter x2x1_lshifter_1 (.ShiftIn(ShiftIn), .A(A[1:0]), .shift(shift), .O(O[1:0]));
  x2x1_Lshifter x2x1_lshifter_2 (.ShiftIn(A[1]), .A(A[3:2]), .shift(shift), .O(O[3:2]));
endmodule

module x4x2_Lshifter (
  input  [3:0] A,
  input  [1:0] shamt,
  output [3:0] O
);

  wire or_1_out, or_2_out, x2_decoder_1_o1, x2_decoder_1_o2, x2_decoder_1_o3;
  wire [3:0] x4x1_lshifter_1_o, x4x1_lshifter_2_o;

  x2_decoder x2_decoder_1 (
    .i0(shamt[0]), .i1(shamt[1]), .o1(x2_decoder_1_o1), .o2(x2_decoder_1_o2), .o3(x2_decoder_1_o3));  // open: o0
  or or_1 (or_1_out, x2_decoder_1_o1, x2_decoder_1_o2, x2_decoder_1_o3);
  x4x1_Lshifter x4x1_lshifter_1 (.ShiftIn(1'b0), .A(A), .shift(or_1_out), .O(x4x1_lshifter_1_o));
  or or_2 (or_2_out, x2_decoder_1_o2, x2_decoder_1_o3);
  x4x1_Lshifter x4x1_lshifter_2 (.ShiftIn(1'b0), .A(x4x1_lshifter_1_o), .shift(or_2_out), .O(x4x1_lshifter_2_o));
  x4x1_Lshifter x4x1_lshifter_3 (.ShiftIn(1'b0), .A(x4x1_lshifter_2_o), .shift(x2_decoder_1_o3), .O(O));
endmodule

module x4x1_RLshifter (
  input  Right,
  input  ShiftIn,
  input  [3:0] A,
  input  shift,
  output [3:0] O
);

  wire [1:0] x2x1_lshifter_1_o, x2x1_lshifter_2_o;
  wire [3:0] multiplexer_1_out, x4_reverse_1_out_2, x4_reverse_2_out_2;

  Multiplexer #(.width(4)) multiplexer_1 (.in0(A), .in1(x4_reverse_1_out_2), .out(multiplexer_1_out), .sel(Right));
  x4_reverse x4_reverse_1 (.in_1(A), .out_2(x4_reverse_1_out_2));
  x2x1_Lshifter x2x1_lshifter_1 (.ShiftIn(ShiftIn), .A(multiplexer_1_out[1:0]), .shift(shift), .O(x2x1_lshifter_1_o));
  x2x1_Lshifter x2x1_lshifter_2 (
    .ShiftIn(multiplexer_1_out[1]), .A(multiplexer_1_out[3:2]), .shift(shift), .O(x2x1_lshifter_2_o));
  x4_reverse x4_reverse_2 (.in_1({x2x1_lshifter_2_o, x2x1_lshifter_1_o}), .out_2(x4_reverse_2_out_2));
  Multiplexer #(.width(4)) multiplexer_2 (
    .in0({x2x1_lshifter_2_o, x2x1_lshifter_1_o}), .in1(x4_reverse_2_out_2), .out(O), .sel(Right));

  // Notes on the sheet:
  //   A right shift is the formula reverse(Lshift(reverse(A), n))
endmodule

module x4x1_RLshifter_arith (
  input  Right,
  input  Arith,
  input  [3:0] A,
  input  Shift,
  output [3:0] O
);

  wire and_1_out, and_2_out;

  and and_1 (and_1_out, Arith, Right);
  and and_2 (and_2_out, and_1_out, A[3]);
  x4x1_RLshifter x4x1_rlshifter_1 (.Right(Right), .ShiftIn(and_2_out), .A(A), .shift(Shift), .O(O));

  // Notes on the sheet:
  //   To perform an arithmatic shift (retain the sign bit)
endmodule

module x4x2_RLshifter_arith (
  input  in_1,
  input  in_2,
  input  [3:0] in_3,
  input  [1:0] in_4,
  output [3:0] out_5
);

  wire or_1_out, or_2_out, x2_decoder_1_o1, x2_decoder_1_o2, x2_decoder_1_o3;
  wire [3:0] x4x1_rlshifter_1_o, x4x1_rlshifter_arith_1_o;

  or or_1 (or_1_out, x2_decoder_1_o1, x2_decoder_1_o2, x2_decoder_1_o3);
  x2_decoder x2_decoder_1 (
    .i0(in_4[0]), .i1(in_4[1]), .o1(x2_decoder_1_o1), .o2(x2_decoder_1_o2), .o3(x2_decoder_1_o3));  // open: o0
  x4x1_RLshifter_arith x4x1_rlshifter_arith_1 (
    .Right(in_1), .Arith(in_2), .A(in_3), .Shift(or_1_out), .O(x4x1_rlshifter_arith_1_o));
  or or_2 (or_2_out, x2_decoder_1_o2, x2_decoder_1_o3);
  x4x1_RLshifter x4x1_rlshifter_1 (
    .Right(in_1), .A(x4x1_rlshifter_arith_1_o), .shift(or_2_out), .O(x4x1_rlshifter_1_o));  // open: ShiftIn
  x4x1_RLshifter x4x1_rlshifter_2 (
    .Right(in_1), .A(x4x1_rlshifter_1_o), .shift(x2_decoder_1_o3), .O(out_5));  // open: ShiftIn

  // Notes on the sheet:
  //   Note here only the very first shifter needs to be aware this is arithmatic
endmodule

module x1_decoder (
  input  A,
  output o0,
  output o1
);

  not not_1 (o0, A);

  assign o1 = A;
endmodule

module x2_decoder (
  input  i0,
  input  i1,
  output o0,
  output o1,
  output o2,
  output o3
);

  wire x1_decoder_1_o0, x1_decoder_1_o1, x1_decoder_2_o0, x1_decoder_2_o1;

  x1_decoder x1_decoder_1 (.A(i0), .o0(x1_decoder_1_o0), .o1(x1_decoder_1_o1));
  x1_decoder x1_decoder_2 (.A(i1), .o0(x1_decoder_2_o0), .o1(x1_decoder_2_o1));
  and and_1 (o0, x1_decoder_1_o0, x1_decoder_2_o0);
  and and_2 (o1, x1_decoder_1_o1, x1_decoder_2_o0);
  and and_3 (o2, x1_decoder_1_o0, x1_decoder_2_o1);
  and and_4 (o3, x1_decoder_1_o1, x1_decoder_2_o1);
endmodule

module x4_decoder (
  input  in_1,
  input  in_2,
  input  in_3,
  input  in_4,
  output out_5,
  output out_6,
  output out_7,
  output out_8,
  output out_9,
  output out_10,
  output out_11,
  output out_12,
  output out_13,
  output out_14,
  output out_15,
  output out_16,
  output out_17,
  output out_18,
  output out_19,
  output out_20
);

  wire x2_decoder_1_o0, x2_decoder_1_o1, x2_decoder_1_o2, x2_decoder_1_o3, x2_decoder_2_o0, x2_decoder_2_o1,
       x2_decoder_2_o2, x2_decoder_2_o3;

  x2_decoder x2_decoder_1 (
    .i0(in_1), .i1(in_2), .o0(x2_decoder_1_o0), .o1(x2_decoder_1_o1), .o2(x2_decoder_1_o2),
    .o3(x2_decoder_1_o3));
  x2_decoder x2_decoder_2 (
    .i0(in_3), .i1(in_4), .o0(x2_decoder_2_o0), .o1(x2_decoder_2_o1), .o2(x2_decoder_2_o2),
    .o3(x2_decoder_2_o3));
  and and_1 (out_5, x2_decoder_1_o0, x2_decoder_2_o0);
  and and_2 (out_6, x2_decoder_1_o1, x2_decoder_2_o0);
  and and_3 (out_7, x2_decoder_1_o2, x2_decoder_2_o0);
  and and_4 (out_8, x2_decoder_1_o3, x2_decoder_2_o0);
  and and_5 (out_9, x2_decoder_1_o0, x2_decoder_2_o1);
  and and_6 (out_10, x2_decoder_1_o1, x2_decoder_2_o1);
  and and_7 (out_11, x2_decoder_1_o2, x2_decoder_2_o1);
  and and_8 (out_12, x2_decoder_1_o3, x2_decoder_2_o1);
  and and_9 (out_13, x2_decoder_1_o0, x2_decoder_2_o2);
  and and_10 (out_14, x2_decoder_1_o1, x2_decoder_2_o2);
  and and_11 (out_15, x2_decoder_1_o2, x2_decoder_2_o2);
  and and_12 (out_16, x2_decoder_1_o3, x2_decoder_2_o2);
  and and_13 (out_17, x2_decoder_1_o0, x2_decoder_2_o3);
  and and_14 (out_18, x2_decoder_1_o1, x2_decoder_2_o3);
  and and_15 (out_19, x2_decoder_1_o2, x2_decoder_2_o3);
  and and_16 (out_20, x2_decoder_1_o3, x2_decoder_2_o3);

  // Notes on the sheet:
  //   Decoders Grow Very Quickly
  //   They also do not chain as cleanly as MUXs
endmodule

module x2_reverse (
  input  [1:0] A,
  output [1:0] O
);


  assign O = {A[0], A[1]};
endmodule

module x4_reverse (
  input  [3:0] in_1,
  output [3:0] out_2
);


  assign out_2 = {in_1[0], in_1[1], in_1[2], in_1[3]};

  // Notes on the sheet:
  //   we have to cross the streams
endmodule

module x32_reverse (
  input  [31:0] in_1,
  output [31:0] out_2
);


  assign out_2 = {in_1[0], in_1[1], in_1[2], in_1[3], in_1[4], in_1[5], in_1[6], in_1[7], in_1[8], in_1[9], in_1[10], in_1[11], in_1[12], in_1[13], in_1[14], in_1[15], in_1[16], in_1[17], in_1[18], in_1[19], in_1[20], in_1[21], in_1[22], in_1[23], in_1[24], in_1[25], in_1[26], in_1[27], in_1[28], in_1[29], in_1[30], in_1[31]};
endmodule

module test (
  input  in_1,
  input  in_2,
  input  in_3,
  output out_4,
  output out_5,
  output out_6,
  output out_7,
  output out_8,
  output out_9,
  output out_10,
  output out_11
);

  wire x1_decoder_1_o0, x1_decoder_1_o1, x2_decoder_1_o0, x2_decoder_1_o1, x2_decoder_1_o2, x2_decoder_1_o3;

  x2_decoder x2_decoder_1 (
    .i0(in_1), .i1(in_2), .o0(x2_decoder_1_o0), .o1(x2_decoder_1_o1), .o2(x2_decoder_1_o2),
    .o3(x2_decoder_1_o3));
  x1_decoder x1_decoder_1 (.A(in_3), .o0(x1_decoder_1_o0), .o1(x1_decoder_1_o1));
  and and_1 (out_4, x2_decoder_1_o0, x1_decoder_1_o0);
  and and_2 (out_5, x2_decoder_1_o1, x1_decoder_1_o0);
  and and_3 (out_6, x2_decoder_1_o2, x1_decoder_1_o0);
  and and_4 (out_7, x2_decoder_1_o3, x1_decoder_1_o0);
  and and_5 (out_8, x2_decoder_1_o0, x1_decoder_1_o1);
  and and_6 (out_9, x2_decoder_1_o1, x1_decoder_1_o1);
  and and_7 (out_10, x2_decoder_1_o2, x1_decoder_1_o1);
  and and_8 (out_11, x2_decoder_1_o3, x1_decoder_1_o1);
endmodule

module test2 (
  input  a,
  input  b,
  input  c,
  output o
);

  wire and_1_out, and_2_out, and_3_out, and_4_out, and_5_out, and_6_out, not_1_out, not_2_out, not_3_out,
       or_1_out;

  not not_1 (not_1_out, a);
  not not_2 (not_2_out, b);
  not not_3 (not_3_out, c);
  and and_1 (and_1_out, not_1_out, not_2_out);
  and and_2 (and_2_out, and_1_out, c);
  and and_3 (and_3_out, not_1_out, b);
  and and_4 (and_4_out, and_3_out, not_3_out);
  and and_5 (and_5_out, a, not_2_out);
  or or_1 (or_1_out, and_2_out, and_4_out);
  and and_6 (and_6_out, and_5_out, not_3_out);
  or or_2 (o, or_1_out, and_6_out);
endmodule
