// Logisim project mipsCpu.circ as structural Verilog: 2 circuits, main circuit registers_alu
module registers_alu (
  input  [5:0] funct,
  input  [4:0] shamt,
  input  [4:0] readAddr1,
  input  [4:0] readAddr2,
  input  Clk,
  input  WriteEnable,
  input  [4:0] writeAddr,
  input  [31:0] setRegData,
  input  setReg,
  output [31:0] readData1,
  output [31:0] readData2
);

  wire [31:0] alu_and_controller_1_o, multiplexer_1_out;

  Multiplexer #(.width(32)) multiplexer_1 (
    .in0(alu_and_controller_1_o), .in1(setRegData), .out(multiplexer_1_out), .sel(setReg));
  x32_32_registerFile x32_32_registerfile_1 (
    .readAddr1(readAddr1), .readAddr2(readAddr2), .Clk(Clk), .WriteEnable(WriteEnable),
    .writeAddr(writeAddr), .writeData(multiplexer_1_out), .readData1(readData1), .readData2(readData2));
  alu_and_controller alu_and_controller_1 (
    .funt(funct), .shamt(shamt), .A(readData1), .B(readData2), .O(alu_and_controller_1_o));  // open: Z, C, V

  // Notes on the sheet:
  //   For convience this will let you set a register to a value
  //   By combining out register file we can now read and write to our 32 registers by setting inputs
  //   And this will let you peek at the data in the registers
endmodule

module op_decoder (
  input  [31:0] instr,
  output [5:0] op,
  output [4:0] rs,
  output [4:0] rt,
  output [4:0] rd,
  output [4:0] shamat,
  output [5:0] funct,
  output [15:0] imm,
  output [25:0] addr
);


  assign funct = instr[31:26];
  assign op = instr[5:0];
  assign rd = instr[20:16];
  assign rs = instr[10:6];
  assign rt = instr[15:11];
  assign shamat = instr[25:21];
endmodule
