// Logisim project registers.circ as structural Verilog: 14 circuits, main circuit x4_siso_shift_reg
module x4_pipo_reg (
  input  [3:0] I,
  input  Clk,
  output [3:0] O
);

  D_Flip_Flop x3 (.D(I[3]), .clk(Clk), .Q(O[3]));  // open: Qn, preset, reset
  D_Flip_Flop x2 (.D(I[2]), .clk(Clk), .Q(O[2]));  // open: Qn, preset, reset
  D_Flip_Flop x1 (.D(I[1]), .clk(Clk), .Q(O[1]));  // open: Qn, preset, reset
  D_Flip_Flop x0 (.D(I[0]), .clk(Clk), .Q(O[0]));  // open: Qn, preset, reset

  // Notes on the sheet:
  //   I - input
  //   O - output
  //   Clk - clock signal
  //   One of the simpliest register designs just writes data on clock and output is the current d-flip-flop contents
endmodule

module x8_pipo_reg (
  input  [7:0] I,
  input  Clk,
  output [7:0] O
);

  x4_pipo_reg x7_4 (.I(I[7:4]), .Clk(Clk), .O(O[7:4]));
  x4_pipo_reg x3_0 (.I(I[3:0]), .Clk(Clk), .O(O[3:0]));
endmodule

module x16_pipo_reg (
  input  [15:0] I,
  input  Clk,
  output [15:0] O
);

  x8_pipo_reg x15_8 (.I(I[15:8]), .Clk(Clk), .O(O[15:8]));
  x8_pipo_reg x7_0 (.I(I[7:0]), .Clk(Clk), .O(O[7:0]));
endmodule

module x32_pipo_reg (
  input  [31:0] I,
  input  Clk,
  output [31:0] O
);

  x16_pipo_reg x31_16 (.I(I[31:16]), .Clk(Clk), .O(O[31:16]));
  x16_pipo_reg x15_0 (.I(I[15:0]), .Clk(Clk), .O(O[15:0]));
endmodule

module x4_siso_shift_reg (
  input  S,
  input  I,
  input  Clk,
  input  E,
  input  R,
  output O
);

  wire and_1_out, x1_q, x2_q, x3_q;

  D_Flip_Flop x3 (.D(I), .clk(and_1_out), .Q(x3_q), .preset(S), .reset(R));  // open: Qn
  and and_1 (and_1_out, Clk, E);
  D_Flip_Flop x2 (.D(x3_q), .clk(and_1_out), .Q(x2_q), .preset(S), .reset(R));  // open: Qn
  D_Flip_Flop x1 (.D(x2_q), .clk(and_1_out), .Q(x1_q), .preset(S), .reset(R));  // open: Qn
  D_Flip_Flop x0 (.D(x1_q), .clk(and_1_out), .Q(O), .preset(S), .reset(R));  // open: Qn

  // Notes on the sheet:
  //   E enable
  //   I input
  //   O output
  //   serial in serial out
  //   every clock pulse writes I to x3
  //   moves data from xN to xN-1
  //   O is the current value of x0
  //   bits shifted out of x0 are gone
  //   S sets all memory to 1 async
  //   R sets all memory to 0 async
endmodule

module x8_siso_shift_reg (
  input  S,
  input  I,
  input  Clk,
  input  E,
  input  R,
  output O
);

  wire x7_4_o;

  x4_siso_shift_reg x7_4 (.S(S), .I(I), .Clk(Clk), .E(E), .R(R), .O(x7_4_o));
  x4_siso_shift_reg x3_0 (.S(S), .I(x7_4_o), .Clk(Clk), .E(E), .R(R), .O(O));

  // Notes on the sheet:
  //   Like many things these are easily chained
endmodule

module x4_sipo_shift_reg (
  input  S,
  input  I,
  input  Clk,
  input  E,
  input  R,
  output [3:0] O
);

  wire and_1_out;

  D_Flip_Flop x3 (.D(I), .clk(and_1_out), .Q(O[3]), .preset(S), .reset(R));  // open: Qn
  and and_1 (and_1_out, Clk, E);
  D_Flip_Flop x2 (.D(O[3]), .clk(and_1_out), .Q(O[2]), .preset(S), .reset(R));  // open: Qn
  D_Flip_Flop x1 (.D(O[2]), .clk(and_1_out), .Q(O[1]), .preset(S), .reset(R));  // open: Qn
  D_Flip_Flop x0 (.D(O[1]), .clk(and_1_out), .Q(O[0]), .preset(S), .reset(R));  // open: Qn

  // Notes on the sheet:
  //   E enable
  //   I input
  //   O output
  //   serial in parallel out
  //   every clock pulse writes I to x3
  //   moves data from xN to xN-1
  //   O is the current value of all cells
  //   bits shifted out of x0 are gone
  //   S sets all memory to 1 async
  //   R sets all memory to 0 async
endmodule

module x4_piso_shift_reg (
  input  [3:0] I,
  input  Shift,
  input  S,
  input  Clk,
  input  E,
  input  R,
  output O
);

  wire and_1_out, multiplexer_1_out, multiplexer_2_out, multiplexer_3_out, multiplexer_4_out, x1_q, x2_q,
       x3_q;

  Multiplexer multiplexer_1 (.in0(I[3]), .in1(1'b0), .out(multiplexer_1_out));  // open: sel
  and and_1 (and_1_out, Clk, E);
  D_Flip_Flop x3 (.D(multiplexer_1_out), .clk(and_1_out), .Q(x3_q), .preset(S), .reset(R));  // open: Qn
  Multiplexer multiplexer_2 (.in0(I[2]), .in1(x3_q), .out(multiplexer_2_out));  // open: sel
  D_Flip_Flop x2 (.D(multiplexer_2_out), .clk(and_1_out), .Q(x2_q), .preset(S), .reset(R));  // open: Qn
  Multiplexer multiplexer_3 (.in0(I[1]), .in1(x2_q), .out(multiplexer_3_out));  // open: sel
  D_Flip_Flop x1 (.D(multiplexer_3_out), .clk(and_1_out), .Q(x1_q), .preset(S), .reset(R));  // open: Qn
  Multiplexer multiplexer_4 (.in0(I[0]), .in1(x1_q), .out(multiplexer_4_out));  // open: sel
  D_Flip_Flop x0 (.D(multiplexer_4_out), .clk(and_1_out), .Q(O), .preset(S), .reset(R));  // open: Qn

  // Notes on the sheet:
  //   E enable
  //   I input
  //   O output
  //   parellel in serial out
  //   if Shift is not set
  //   if Shift is set
  //   S sets all memory to 1 async
  //   R sets all memory to 0 async
  //   every clock pulse writes I to x3-0
  //   moves data from xN to xN-1
  //   bits shifted out of x0 are gone
  //   O is the current value of x0
  //   Shift off write data from I; on shift data down
endmodule

module x4_pipo_shift_reg (
  input  [3:0] I,
  input  Shift,
  input  S,
  input  Clk,
  input  E,
  input  R,
  output [3:0] O
);

  wire and_1_out, multiplexer_1_out, multiplexer_2_out, multiplexer_3_out, multiplexer_4_out;

  Multiplexer multiplexer_1 (.in0(I[3]), .in1(1'b0), .out(multiplexer_1_out));  // open: sel
  and and_1 (and_1_out, Clk, E);
  D_Flip_Flop x3 (.D(multiplexer_1_out), .clk(and_1_out), .Q(O[3]), .preset(S), .reset(R));  // open: Qn
  Multiplexer multiplexer_2 (.in0(I[2]), .in1(O[3]), .out(multiplexer_2_out));  // open: sel
  D_Flip_Flop x2 (.D(multiplexer_2_out), .clk(and_1_out), .Q(O[2]), .preset(S), .reset(R));  // open: Qn
  Multiplexer multiplexer_3 (.in0(I[1]), .in1(O[2]), .out(multiplexer_3_out));  // open: sel
  D_Flip_Flop x1 (.D(multiplexer_3_out), .clk(and_1_out), .Q(O[1]), .preset(S), .reset(R));  // open: Qn
  Multiplexer multiplexer_4 (.in0(I[0]), .in1(O[1]), .out(multiplexer_4_out));  // open: sel
  D_Flip_Flop x0 (.D(multiplexer_4_out), .clk(and_1_out), .Q(O[0]), .preset(S), .reset(R));  // open: Qn

  // Notes on the sheet:
  //   E enable
  //   I input
  //   O output
  //   parellel in parellel out
  //   if Shift is not set
  //   if Shift is set
  //   S sets all memory to 1 async
  //   R sets all memory to 0 async
  //   every clock pulse writes I to x3-0
  //   moves data from xN to xN-1
  //   bits shifted out of x0 are gone
  //   O is the current value of x3-0
  //   Shift off write data from I; on shift data down
endmodule

module x4_pipo_bi_shift_reg (
  input  [3:0] I,
  input  Shift,
  input  Left,
  input  S,
  input  Clk,
  input  E,
  input  R,
  output O0,
  output O3
);

  wire and_1_out, multiplexer_1_out, multiplexer_2_out, multiplexer_3_out, multiplexer_4_out, x1_q, x2_q;

  and and_1 (and_1_out, Clk, E);
  Multiplexer #(.select(2)) multiplexer_1 (
    .in0(I[3]), .in1(1'b0), .in2(I[0]), .in3(x2_q), .out(multiplexer_1_out));  // open: sel
  D_Flip_Flop x3 (.D(multiplexer_1_out), .clk(and_1_out), .Q(O3), .preset(S), .reset(R));  // open: Qn
  Multiplexer #(.select(2)) multiplexer_2 (
    .in0(I[2]), .in1(O3), .in2(I[1]), .in3(x1_q), .out(multiplexer_2_out));  // open: sel
  D_Flip_Flop x2 (.D(multiplexer_2_out), .clk(and_1_out), .Q(x2_q), .preset(S), .reset(R));  // open: Qn
  Multiplexer #(.select(2)) multiplexer_3 (
    .in0(I[1]), .in1(x2_q), .in2(I[2]), .in3(O0), .out(multiplexer_3_out));  // open: sel
  D_Flip_Flop x1 (.D(multiplexer_3_out), .clk(and_1_out), .Q(x1_q), .preset(S), .reset(R));  // open: Qn
  Multiplexer #(.select(2)) multiplexer_4 (
    .in0(I[0]), .in1(x1_q), .in2(I[3]), .in3(1'b0), .out(multiplexer_4_out));  // open: sel
  D_Flip_Flop x0 (.D(multiplexer_4_out), .clk(and_1_out), .Q(O0), .preset(S), .reset(R));  // open: Qn

  // Notes on the sheet:
  //   if Shift is set
  //   O0 is x0; O3 is x3
  //   E enable
  //   I input
  //   bi-directional parellel in serial out
  //   if Shift and Left are not set
  //   If Left and not Shift
  //   moves data from xN to xN-1
  //   bits shifted out of x0 are gone
  //   if Shift and Left is set
  //   moves data from xN to xN+1
  //   bits shifted out of x0 are gone
  //   S sets all memory to 1 async
  //   R sets all memory to 0 async
  //   O0/3 output
  //   every clock pulse writes I to x3-0
  //   every clock pulse writes I to x0-3
  //   Shift off write data from I; on shift data down
  //   Left off shift data right if shifting; on shift data left if shifting
  //   This wireing is getting messy isnt it
endmodule

module x4_universal_shift_reg (
  input  [3:0] I,
  input  Shift,
  input  Left,
  input  S,
  input  Clk,
  input  E,
  input  R,
  output O0,
  output O3,
  output [3:0] O,
  output [3:0] revO
);

  wire and_1_out, multiplexer_1_out, multiplexer_2_out, multiplexer_3_out, multiplexer_4_out;

  and and_1 (and_1_out, Clk, E);
  Multiplexer #(.select(2)) multiplexer_1 (
    .in0(I[3]), .in1(I[0]), .in2(I[0]), .in3(O[2]), .out(multiplexer_1_out));  // open: sel
  D_Flip_Flop x3 (.D(multiplexer_1_out), .clk(and_1_out), .Q(O[3]), .preset(S), .reset(R));  // open: Qn
  Multiplexer #(.select(2)) multiplexer_2 (
    .in0(I[2]), .in1(O[3]), .in2(I[1]), .in3(O[1]), .out(multiplexer_2_out));  // open: sel
  D_Flip_Flop x2 (.D(multiplexer_2_out), .clk(and_1_out), .Q(O[2]), .preset(S), .reset(R));  // open: Qn
  Multiplexer #(.select(2)) multiplexer_3 (
    .in0(I[1]), .in1(O[2]), .in2(I[2]), .in3(O[0]), .out(multiplexer_3_out));  // open: sel
  D_Flip_Flop x1 (.D(multiplexer_3_out), .clk(and_1_out), .Q(O[1]), .preset(S), .reset(R));  // open: Qn
  Multiplexer #(.select(2)) multiplexer_4 (
    .in0(I[0]), .in1(O[1]), .in2(I[3]), .in3(I[0]), .out(multiplexer_4_out));  // open: sel
  D_Flip_Flop x0 (.D(multiplexer_4_out), .clk(and_1_out), .Q(O[0]), .preset(S), .reset(R));  // open: Qn

  assign O0 = O[0];
  assign O3 = O[3];
  assign revO = {O[0], O[1], O[2], O[3]};

  // Notes on the sheet:
  //   I input
  //   UNIVERSAL
  //   if Shift is not set
  //   if Left is set
  //   if Shift is set
  //   if Shift and Left is set
  //   O0 is x0; O3 is x3
  //   E enable
  //   O* output
  //   every clock pulse writes I to x0-3
  //   every clock pulse write I to 0x3-0
  //   bit 1 of I is writen to x0
  //   moves data from xN to xN+1
  //   bits shifted out of x3 are gone
  //   bit 1 of I is writen to x3
  //   moves data from xN to xN-1
  //   bits shifted out of x0 are gone
  //   S sets all memory to 1 async
  //   R sets all memory to 0 async
  //   Left swap direction of writing and shifting
  //   O is parellel read; revO is parellel read in reverse order
  //   Shift off write data from I; on shift data down write bit 1 of I
  //   Can we make on that does everything, yes but its gonna be messy
endmodule

module x8_univseral_shift_reg (
  input  [7:0] in_1,
  input  in_2,
  input  in_3,
  input  in_4,
  input  in_5,
  input  in_6,
  input  in_7,
  output O0,
  output O7,
  output [7:0] O,
  output [7:0] revO
);

  wire [0:0] x3_0_o3, x7_4_o0;
  wire [3:0] multiplexer_1_out, multiplexer_2_out;

  Multiplexer #(.select(2), .width(4)) multiplexer_1 (
    .in0(in_1[7:4]), .in1(in_1[3:0]), .in2(in_1[3:0]), .in3({3'b000, x3_0_o3[0]}), .out(multiplexer_1_out),
    .sel({in_3, in_2}));
  x4_universal_shift_reg x7_4 (
    .I(multiplexer_1_out), .Shift(in_2), .Left(in_3), .S(in_4), .Clk(in_5), .E(in_6), .R(in_7),
    .O0(x7_4_o0[0]), .O3(O7), .O(O[7:4]), .revO(revO[3:0]));
  Multiplexer #(.select(2), .width(4)) multiplexer_2 (
    .in0(in_1[3:0]), .in1({3'b000, x7_4_o0[0]}), .in2(in_1[7:4]), .in3(in_1[3:0]), .out(multiplexer_2_out),
    .sel({in_3, in_2}));
  x4_universal_shift_reg x3_0 (
    .I(multiplexer_2_out), .Shift(in_2), .Left(in_3), .S(in_4), .Clk(in_5), .E(in_6), .R(in_7), .O0(O0),
    .O3(x3_0_o3[0]), .O(O[3:0]), .revO(revO[7:4]));

  // Notes on the sheet:
  //   Chaining these together is not quite as simple and requires some mux's
  //   Note however they are wired up more or less the same as the mux's from the x4 version
endmodule

module x32_4_RegisterFile (
  input  [1:0] readAddr1,
  input  [1:0] readAddr2,
  input  Clk,
  input  WriteEnable,
  input  [1:0] writeAddr,
  input  [31:0] writeData,
  output [31:0] readData1,
  output [31:0] readData2
);

  wire and_1_out, decoder_1_out0, decoder_1_out1, decoder_1_out2, decoder_1_out3;
  wire [31:0] reg0_o, reg1_o, reg2_o, reg3_o;

  and and_1 (and_1_out, Clk, WriteEnable);
  Decoder #(.select(2)) decoder_1 (
    .out0(decoder_1_out0), .out1(decoder_1_out1), .out2(decoder_1_out2), .out3(decoder_1_out3),
    .sel(writeAddr), .en(and_1_out));
  x32_pipo_reg reg0 (.I(writeData), .Clk(decoder_1_out0), .O(reg0_o));
  x32_pipo_reg reg1 (.I(writeData), .Clk(decoder_1_out1), .O(reg1_o));
  x32_pipo_reg reg2 (.I(writeData), .Clk(decoder_1_out2), .O(reg2_o));
  x32_pipo_reg reg3 (.I(writeData), .Clk(decoder_1_out3), .O(reg3_o));
  Multiplexer #(.select(2), .width(32)) multiplexer_1 (
    .in0(reg0_o), .in1(reg1_o), .in2(reg2_o), .in3(reg3_o), .out(readData1));  // open: sel
  Multiplexer #(.select(2), .width(32)) multiplexer_2 (
    .in0(reg0_o), .in1(reg1_o), .in2(reg2_o), .in3(reg3_o), .out(readData2));  // open: sel
endmodule

module x32_32_registerFile (
  input  [4:0] readAddr1,
  input  [4:0] readAddr2,
  input  Clk,
  input  WriteEnable,
  input  [4:0] writeAddr,
  input  [31:0] writeData,
  output [31:0] readData1,
  output [31:0] readData2
);

  wire and_1_out, decoder_1_out1, decoder_1_out2, decoder_1_out3, decoder_1_out4, decoder_1_out5,
       decoder_1_out6, decoder_1_out7, decoder_1_out8, decoder_1_out9, decoder_1_out10, decoder_1_out11,
       decoder_1_out12, decoder_1_out13, decoder_1_out14, decoder_1_out15, decoder_1_out16, decoder_1_out17,
       decoder_1_out18, decoder_1_out19, decoder_1_out20, decoder_1_out21, decoder_1_out22, decoder_1_out23,
       decoder_1_out24, decoder_1_out25, decoder_1_out26, decoder_1_out27, decoder_1_out28, decoder_1_out29,
       decoder_1_out30, decoder_1_out31;
  wire [31:0] r1_at_q, r2_v0_q, r3_v1_q, r4_a0_q, r5_a1_q, r6_a2_q, r7_a3_q, r8_t0_q, r9_t1_q, r10_t2_q,
       r11_t3_q, r12_t4_q, r13_t5_q, r14_t6_q, r15_t7_q, r16_s0_q, r17_s1_q, r18_s2_q, r19_s3_q, r20_s4_q,
       r21_s5_q, r22_s6_q, r23_s7_q, r24_t8_q, r25_t9_q, r26_k0_q, r27_k1_q, r28_gp_q, r29_sp_q, r30_fp_q,
       r31_ra_q;

  Decoder #(.enable("false"), .select(5)) decoder_1 (
    .out1(decoder_1_out1), .out2(decoder_1_out2), .out3(decoder_1_out3), .out4(decoder_1_out4),
    .out5(decoder_1_out5), .out6(decoder_1_out6), .out7(decoder_1_out7), .out8(decoder_1_out8),
    .out9(decoder_1_out9), .out10(decoder_1_out10), .out11(decoder_1_out11), .out12(decoder_1_out12),
    .out13(decoder_1_out13), .out14(decoder_1_out14), .out15(decoder_1_out15), .out16(decoder_1_out16),
    .out17(decoder_1_out17), .out18(decoder_1_out18), .out19(decoder_1_out19), .out20(decoder_1_out20),
    .out21(decoder_1_out21), .out22(decoder_1_out22), .out23(decoder_1_out23), .out24(decoder_1_out24),
    .out25(decoder_1_out25), .out26(decoder_1_out26), .out27(decoder_1_out27), .out28(decoder_1_out28),
    .out29(decoder_1_out29), .out30(decoder_1_out30), .out31(decoder_1_out31), .sel(writeAddr));  // open: out0
  and and_1 (and_1_out, Clk, WriteEnable);
  Register #(.width(32)) r1_at (.D(writeData), .en(decoder_1_out1), .clk(and_1_out), .Q(r1_at_q));  // open: clr
  Register #(.width(32)) r2_v0 (.D(writeData), .en(decoder_1_out2), .clk(and_1_out), .Q(r2_v0_q));  // open: clr
  Register #(.width(32)) r3_v1 (.D(writeData), .en(decoder_1_out3), .clk(and_1_out), .Q(r3_v1_q));  // open: clr
  Register #(.width(32)) r4_a0 (.D(writeData), .en(decoder_1_out4), .clk(and_1_out), .Q(r4_a0_q));  // open: clr
  Register #(.width(32)) r5_a1 (.D(writeData), .en(decoder_1_out5), .clk(and_1_out), .Q(r5_a1_q));  // open: clr
  Register #(.width(32)) r6_a2 (.D(writeData), .en(decoder_1_out6), .clk(and_1_out), .Q(r6_a2_q));  // open: clr
  Register #(.width(32)) r7_a3 (.D(writeData), .en(decoder_1_out7), .clk(and_1_out), .Q(r7_a3_q));  // open: clr
  Register #(.width(32)) r8_t0 (.D(writeData), .en(decoder_1_out8), .clk(and_1_out), .Q(r8_t0_q));  // open: clr
  Register #(.width(32)) r9_t1 (.D(writeData), .en(decoder_1_out9), .clk(and_1_out), .Q(r9_t1_q));  // open: clr
  Register #(.width(32)) r10_t2 (.D(writeData), .en(decoder_1_out10), .clk(and_1_out), .Q(r10_t2_q));  // open: clr
  Register #(.width(32)) r11_t3 (.D(writeData), .en(decoder_1_out11), .clk(and_1_out), .Q(r11_t3_q));  // open: clr
  Register #(.width(32)) r12_t4 (.D(writeData), .en(decoder_1_out12), .clk(and_1_out), .Q(r12_t4_q));  // open: clr
  Register #(.width(32)) r13_t5 (.D(writeData), .en(decoder_1_out13), .clk(and_1_out), .Q(r13_t5_q));  // open: clr
  Register #(.width(32)) r14_t6 (.D(writeData), .en(decoder_1_out14), .clk(and_1_out), .Q(r14_t6_q));  // open: clr
  Register #(.width(32)) r15_t7 (.D(writeData), .en(decoder_1_out15), .clk(and_1_out), .Q(r15_t7_q));  // open: clr
  Register #(.width(32)) r16_s0 (.D(writeData), .en(decoder_1_out16), .clk(and_1_out), .Q(r16_s0_q));  // open: clr
  Register #(.width(32)) r17_s1 (.D(writeData), .en(decoder_1_out17), .clk(and_1_out), .Q(r17_s1_q));  // open: clr
  Register #(.width(32)) r18_s2 (.D(writeData), .en(decoder_1_out18), .clk(and_1_out), .Q(r18_s2_q));  // open: clr
  Register #(.width(32)) r19_s3 (.D(writeData), .en(decoder_1_out19), .clk(and_1_out), .Q(r19_s3_q));  // open: clr
  Register #(.width(32)) r20_s4 (.D(writeData), .en(decoder_1_out20), .clk(and_1_out), .Q(r20_s4_q));  // open: clr
  Register #(.width(32)) r21_s5 (.D(writeData), .en(decoder_1_out21), .clk(and_1_out), .Q(r21_s5_q));  // open: clr
  Register #(.width(32)) r22_s6 (.D(writeData), .en(decoder_1_out22), .clk(and_1_out), .Q(r22_s6_q));  // open: clr
  Register #(.width(32)) r23_s7 (.D(writeData), .en(decoder_1_out23), .clk(and_1_out), .Q(r23_s7_q));  // open: clr
  Register #(.width(32)) r24_t8 (.D(writeData), .en(decoder_1_out24), .clk(and_1_out), .Q(r24_t8_q));  // open: clr
  Register #(.width(32)) r25_t9 (.D(writeData), .en(decoder_1_out25), .clk(and_1_out), .Q(r25_t9_q));  // open: clr
  Register #(.width(32)) r26_k0 (.D(writeData), .en(decoder_1_out26), .clk(and_1_out), .Q(r26_k0_q));  // open: clr
  Register #(.width(32)) r27_k1 (.D(writeData), .en(decoder_1_out27), .clk(and_1_out), .Q(r27_k1_q));  // open: clr
  Register #(.width(32)) r28_gp (.D(writeData), .en(decoder_1_out28), .clk(and_1_out), .Q(r28_gp_q));  // open: clr
  Register #(.width(32)) r29_sp (.D(writeData), .en(decoder_1_out29), .clk(and_1_out), .Q(r29_sp_q));  // open: clr
  Register #(.width(32)) r30_fp (.D(writeData), .en(decoder_1_out30), .clk(and_1_out), .Q(r30_fp_q));  // open: clr
  Register #(.width(32)) r31_ra (.D(writeData), .en(decoder_1_out31), .clk(and_1_out), .Q(r31_ra_q));  // open: clr
  Multiplexer #(.select(5), .width(32)) multiplexer_1 (
    .in0({32{1'b0}}), .in1(r1_at_q), .in2(r2_v0_q), .in3(r3_v1_q), .in4(r4_a0_q), .in5(r5_a1_q),
    .in6(r6_a2_q), .in7(r7_a3_q), .in8(r8_t0_q), .in9(r9_t1_q), .in10(r10_t2_q), .in11(r11_t3_q),
    .in12(r12_t4_q), .in13(r13_t5_q), .in14(r14_t6_q), .in15(r15_t7_q), .in16(r16_s0_q), .in17(r17_s1_q),
    .in18(r18_s2_q), .in19(r19_s3_q), .in20(r20_s4_q), .in21(r21_s5_q), .in22(r22_s6_q), .in23(r23_s7_q),
    .in24(r24_t8_q), .in25(r25_t9_q), .in26(r26_k0_q), .in27(r27_k1_q), .in28(r28_gp_q), .in29(r29_sp_q),
    .in30(r30_fp_q), .in31(r31_ra_q), .out(readData1));  // open: sel
  Multiplexer #(.select(5), .width(32)) multiplexer_2 (
    .in0({32{1'b0}}), .in1(r1_at_q), .in2(r2_v0_q), .in3(r3_v1_q), .in4(r4_a0_q), .in5(r5_a1_q),
    .in6(r6_a2_q), .in7(r7_a3_q), .in8(r8_t0_q), .in9(r9_t1_q), .in10(r10_t2_q), .in11(r11_t3_q),
    .in12(r12_t4_q), .in13(r13_t5_q), .in14(r14_t6_q), .in15(r15_t7_q), .in16(r16_s0_q), .in17(r17_s1_q),
    .in18(r18_s2_q), .in19(r19_s3_q), .in20(r20_s4_q), .in21(r21_s5_q), .in22(r22_s6_q), .in23(r23_s7_q),
    .in24(r24_t8_q), .in25(r25_t9_q), .in26(r26_k0_q), .in27(r27_k1_q), .in28(r28_gp_q), .in29(r29_sp_q),
    .in30(r30_fp_q), .in31(r31_ra_q), .out(readData2));  // open: sel

  // Notes on the sheet:
  //   switching to logism built ins for performance here
  //   r0_zero
endmodule
