// Logisim project shiftRegisters.circ as structural Verilog: 12 circuits, main circuit x4_siso_shift_reg
module x4_pipo_reg (
  input  [3:0] I,
  input  Clk,
  output [3:0] O
);

  D_Flip_Flop x3 (.D(I[3]), .clk(Clk), .Q(O[3]));  // open: Qn, preset, reset
  D_Flip_Flop x2 (.D(I[2]), .clk(Clk), .Q(O[2]));  // open: Qn, preset, reset
  D_Flip_Flop x1 (.D(I[1]), .clk(Clk), .Q(O[1]));  // open: Qn, preset, reset
  D_Flip_Flop x0 (.D(I[0]), .clk(Clk), .Q(O[0]));  // open: Qn, preset, reset

  // Notes on the sheet:
  //   I - input
  //   O - output
  //   Clk - clock signal
  //   One of the simpliest register designs just writes data on clock and output is the current d-flip-flop contents
endmodule

module x8_pipo_reg (
  input  [7:0] I,
  input  Clk,
  output [7:0] O
);

  x4_pipo_reg x7_4 (.I(I[7:4]), .Clk(Clk), .O(O[7:4]));
  x4_pipo_reg x3_0 (.I(I[3:0]), .Clk(Clk), .O(O[3:0]));
endmodule

module x16_pipo_reg (
  input  [15:0] I,
  input  Clk,
  output [15:0] O
);

  x8_pipo_reg x15_8 (.I(I[15:8]), .Clk(Clk), .O(O[15:8]));
  x8_pipo_reg x7_0 (.I(I[7:0]), .Clk(Clk), .O(O[7:0]));
endmodule

module x32_pipo_reg (
  input  [31:0] I,
  input  Clk,
  output [31:0] O
);

  x16_pipo_reg x31_16 (.I(I[31:16]), .Clk(Clk), .O(O[31:16]));
  x16_pipo_reg x15_0 (.I(I[15:0]), .Clk(Clk), .O(O[15:0]));
endmodule

module x4_siso_shift_reg (
  input  S,
  input  I,
  input  Clk,
  input  E,
  input  R,
  output O
);

  wire and_1_out, x1_q, x2_q, x3_q;

  D_Flip_Flop x3 (.D(I), .clk(and_1_out), .Q(x3_q), .preset(S), .reset(R));  // open: Qn
  and and_1 (and_1_out, Clk, E);
  D_Flip_Flop x2 (.D(x3_q), .clk(and_1_out), .Q(x2_q), .preset(S), .reset(R));  // open: Qn
  D_Flip_Flop x1 (.D(x2_q), .clk(and_1_out), .Q(x1_q), .preset(S), .reset(R));  // open: Qn
  D_Flip_Flop x0 (.D(x1_q), .clk(and_1_out), .Q(O), .preset(S), .reset(R));  // open: Qn

  // Notes on the sheet:
  //   E enable
  //   I input
  //   O output
  //   serial in serial out
  //   every clock pulse writes I to x3
  //   moves data from xN to xN-1
  //   O is the current value of x0
  //   bits shifted out of x0 are gone
  //   S sets all memory to 1 async
  //   R sets all memory to 0 async
endmodule

module x8_siso_shift_reg (
  input  S,
  input  I,
  input  Clk,
  input  E,
  input  R,
  output O
);

  wire x7_4_o;

  x4_siso_shift_reg x7_4 (.S(S), .I(I), .Clk(Clk), .E(E), .R(R), .O(x7_4_o));
  x4_siso_shift_reg x3_0 (.S(S), .I(x7_4_o), .Clk(Clk), .E(E), .R(R), .O(O));

  // Notes on the sheet:
  //   Like many things these are easily chained
endmodule

module x4_sipo_shift_reg (
  input  S,
  input  I,
  input  Clk,
  input  E,
  input  R,
  output [3:0] O
);

  wire and_1_out;

  D_Flip_Flop x3 (.D(I), .clk(and_1_out), .Q(O[3]), .preset(S), .reset(R));  // open: Qn
  and and_1 (and_1_out, Clk, E);
  D_Flip_Flop x2 (.D(O[3]), .clk(and_1_out), .Q(O[2]), .preset(S), .reset(R));  // open: Qn
  D_Flip_Flop x1 (.D(O[2]), .clk(and_1_out), .Q(O[1]), .preset(S), .reset(R));  // open: Qn
  D_Flip_Flop x0 (.D(O[1]), .clk(and_1_out), .Q(O[0]), .preset(S), .reset(R));  // open: Qn

  // Notes on the sheet:
  //   E enable
  //   I input
  //   O output
  //   serial in parallel out
  //   every clock pulse writes I to x3
  //   moves data from xN to xN-1
  //   O is the current value of all cells
  //   bits shifted out of x0 are gone
  //   S sets all memory to 1 async
  //   R sets all memory to 0 async
endmodule

module x4_piso_shift_reg (
  input  [3:0] I,
  input  Shift,
  input  S,
  input  Clk,
  input  E,
  input  R,
  output O
);

  wire and_1_out, multiplexer_1_out, multiplexer_2_out, multiplexer_3_out, multiplexer_4_out, x1_q, x2_q,
       x3_q;

  Multiplexer multiplexer_1 (.in0(I[3]), .in1(1'b0), .out(multiplexer_1_out));  // open: sel
  and and_1 (and_1_out, Clk, E);
  D_Flip_Flop x3 (.D(multiplexer_1_out), .clk(and_1_out), .Q(x3_q), .preset(S), .reset(R));  // open: Qn
  Multiplexer multiplexer_2 (.in0(I[2]), .in1(x3_q), .out(multiplexer_2_out));  // open: sel
  D_Flip_Flop x2 (.D(multiplexer_2_out), .clk(and_1_out), .Q(x2_q), .preset(S), .reset(R));  // open: Qn
  Multiplexer multiplexer_3 (.in0(I[1]), .in1(x2_q), .out(multiplexer_3_out));  // open: sel
  D_Flip_Flop x1 (.D(multiplexer_3_out), .clk(and_1_out), .Q(x1_q), .preset(S), .reset(R));  // open: Qn
  Multiplexer multiplexer_4 (.in0(I[0]), .in1(x1_q), .out(multiplexer_4_out));  // open: sel
  D_Flip_Flop x0 (.D(multiplexer_4_out), .clk(and_1_out), .Q(O), .preset(S), .reset(R));  // open: Qn

  // Notes on the sheet:
  //   E enable
  //   I input
  //   O output
  //   parellel in serial out
  //   if Shift is not set
  //   if Shift is set
  //   S sets all memory to 1 async
  //   R sets all memory to 0 async
  //   every clock pulse writes I to x3-0
  //   moves data from xN to xN-1
  //   bits shifted out of x0 are gone
  //   O is the current value of x0
  //   Shift off write data from I; on shift data down
endmodule

module x4_pipo_shift_reg (
  input  [3:0] I,
  input  Shift,
  input  S,
  input  Clk,
  input  E,
  input  R,
  output [3:0] O
);

  wire and_1_out, multiplexer_1_out, multiplexer_2_out, multiplexer_3_out, multiplexer_4_out;

  Multiplexer multiplexer_1 (.in0(I[3]), .in1(1'b0), .out(multiplexer_1_out));  // open: sel
  and and_1 (and_1_out, Clk, E);
  D_Flip_Flop x3 (.D(multiplexer_1_out), .clk(and_1_out), .Q(O[3]), .preset(S), .reset(R));  // open: Qn
  Multiplexer multiplexer_2 (.in0(I[2]), .in1(O[3]), .out(multiplexer_2_out));  // open: sel
  D_Flip_Flop x2 (.D(multiplexer_2_out), .clk(and_1_out), .Q(O[2]), .preset(S), .reset(R));  // open: Qn
  Multiplexer multiplexer_3 (.in0(I[1]), .in1(O[2]), .out(multiplexer_3_out));  // open: sel
  D_Flip_Flop x1 (.D(multiplexer_3_out), .clk(and_1_out), .Q(O[1]), .preset(S), .reset(R));  // open: Qn
  Multiplexer multiplexer_4 (.in0(I[0]), .in1(O[1]), .out(multiplexer_4_out));  // open: sel
  D_Flip_Flop x0 (.D(multiplexer_4_out), .clk(and_1_out), .Q(O[0]), .preset(S), .reset(R));  // open: Qn

  // Notes on the sheet:
  //   E enable
  //   I input
  //   O output
  //   parellel in parellel out
  //   if Shift is not set
  //   if Shift is set
  //   S sets all memory to 1 async
  //   R sets all memory to 0 async
  //   every clock pulse writes I to x3-0
  //   moves data from xN to xN-1
  //   bits shifted out of x0 are gone
  //   O is the current value of x3-0
  //   Shift off write data from I; on shift data down
endmodule

module x4_pipo_bi_shift_reg (
  input  [3:0] I,
  input  Shift,
  input  Left,
  input  S,
  input  Clk,
  input  E,
  input  R,
  output O0,
  output O3
);

  wire and_1_out, multiplexer_1_out, multiplexer_2_out, multiplexer_3_out, multiplexer_4_out, x1_q, x2_q;

  and and_1 (and_1_out, Clk, E);
  Multiplexer #(.select(2)) multiplexer_1 (
    .in0(I[3]), .in1(1'b0), .in2(I[0]), .in3(x2_q), .out(multiplexer_1_out));  // open: sel
  D_Flip_Flop x3 (.D(multiplexer_1_out), .clk(and_1_out), .Q(O3), .preset(S), .reset(R));  // open: Qn
  Multiplexer #(.select(2)) multiplexer_2 (
    .in0(I[2]), .in1(O3), .in2(I[1]), .in3(x1_q), .out(multiplexer_2_out));  // open: sel
  D_Flip_Flop x2 (.D(multiplexer_2_out), .clk(and_1_out), .Q(x2_q), .preset(S), .reset(R));  // open: Qn
  Multiplexer #(.select(2)) multiplexer_3 (
    .in0(I[1]), .in1(x2_q), .in2(I[2]), .in3(O0), .out(multiplexer_3_out));  // open: sel
  D_Flip_Flop x1 (.D(multiplexer_3_out), .clk(and_1_out), .Q(x1_q), .preset(S), .reset(R));  // open: Qn
  Multiplexer #(.select(2)) multiplexer_4 (
    .in0(I[0]), .in1(x1_q), .in2(I[3]), .in3(1'b0), .out(multiplexer_4_out));  // open: sel
  D_Flip_Flop x0 (.D(multiplexer_4_out), .clk(and_1_out), .Q(O0), .preset(S), .reset(R));  // open: Qn

  // Notes on the sheet:
  //   if Shift is set
  //   O0 is x0; O3 is x3
  //   E enable
  //   I input
  //   bi-directional parellel in serial out
  //   if Shift and Left are not set
  //   If Left and not Shift
  //   moves data from xN to xN-1
  //   bits shifted out of x0 are gone
  //   if Shift and Left is set
  //   moves data from xN to xN+1
  //   bits shifted out of x0 are gone
  //   S sets all memory to 1 async
  //   R sets all memory to 0 async
  //   O0/3 output
  //   every clock pulse writes I to x3-0
  //   every clock pulse writes I to x0-3
  //   Shift off write data from I; on shift data down
  //   Left off shift data right if shifting; on shift data left if shifting
  //   This wireing is getting messy isnt it
endmodule

module x4_universal_shift_reg (
  input  [3:0] I,
  input  Shift,
  input  Left,
  input  S,
  input  Clk,
  input  E,
  input  R,
  output O0,
  output O3,
  output [3:0] O,
  output [3:0] revO
);

  wire and_1_out, multiplexer_1_out, multiplexer_2_out, multiplexer_3_out, multiplexer_4_out;

  and and_1 (and_1_out, Clk, E);
  Multiplexer #(.select(2)) multiplexer_1 (
    .in0(I[3]), .in1(I[0]), .in2(I[0]), .in3(O[2]), .out(multiplexer_1_out));  // open: sel
  D_Flip_Flop x3 (.D(multiplexer_1_out), .clk(and_1_out), .Q(O[3]), .preset(S), .reset(R));  // open: Qn
  Multiplexer #(.select(2)) multiplexer_2 (
    .in0(I[2]), .in1(O[3]), .in2(I[1]), .in3(O[1]), .out(multiplexer_2_out));  // open: sel
  D_Flip_Flop x2 (.D(multiplexer_2_out), .clk(and_1_out), .Q(O[2]), .preset(S), .reset(R));  // open: Qn
  Multiplexer #(.select(2)) multiplexer_3 (
    .in0(I[1]), .in1(O[2]), .in2(I[2]), .in3(O[0]), .out(multiplexer_3_out));  // open: sel
  D_Flip_Flop x1 (.D(multiplexer_3_out), .clk(and_1_out), .Q(O[1]), .preset(S), .reset(R));  // open: Qn
  Multiplexer #(.select(2)) multiplexer_4 (
    .in0(I[0]), .in1(O[1]), .in2(I[3]), .in3(I[0]), .out(multiplexer_4_out));  // open: sel
  D_Flip_Flop x0 (.D(multiplexer_4_out), .clk(and_1_out), .Q(O[0]), .preset(S), .reset(R));  // open: Qn

  assign O0 = O[0];
  assign O3 = O[3];
  assign revO = {O[0], O[1], O[2], O[3]};

  // Notes on the sheet:
  //   I input
  //   UNIVERSAL
  //   if Shift is not set
  //   if Left is set
  //   if Shift is set
  //   if Shift and Left is set
  //   O0 is x0; O3 is x3
  //   E enable
  //   O* output
  //   every clock pulse writes I to x0-3
  //   every clock pulse write I to 0x3-0
  //   bit 1 of I is writen to x0
  //   moves data from xN to xN+1
  //   bits shifted out of x3 are gone
  //   bit 1 of I is writen to x3
  //   moves data from xN to xN-1
  //   bits shifted out of x0 are gone
  //   S sets all memory to 1 async
  //   R sets all memory to 0 async
  //   Left swap direction of writing and shifting
  //   O is parellel read; revO is parellel read in reverse order
  //   Shift off write data from I; on shift data down write bit 1 of I
  //   Can we make on that does everything, yes but its gonna be messy
endmodule

module x8_univseral_shift_reg (
  input  [7:0] in_1,
  input  in_2,
  input  in_3,
  input  in_4,
  input  in_5,
  input  in_6,
  input  in_7,
  output O0,
  output O7,
  output [7:0] O,
  output [7:0] revO
);

  wire [0:0] x3_0_o3, x7_4_o0;
  wire [3:0] multiplexer_1_out, multiplexer_2_out;

  Multiplexer #(.select(2), .width(4)) multiplexer_1 (
    .in0(in_1[7:4]), .in1(in_1[3:0]), .in2(in_1[3:0]), .in3({3'b000, x3_0_o3[0]}), .out(multiplexer_1_out),
    .sel({in_3, in_2}));
  x4_universal_shift_reg x7_4 (
    .I(multiplexer_1_out), .Shift(in_2), .Left(in_3), .S(in_4), .Clk(in_5), .E(in_6), .R(in_7),
    .O0(x7_4_o0[0]), .O3(O7), .O(O[7:4]), .revO(revO[3:0]));
  Multiplexer #(.select(2), .width(4)) multiplexer_2 (
    .in0(in_1[3:0]), .in1({3'b000, x7_4_o0[0]}), .in2(in_1[7:4]), .in3(in_1[3:0]), .out(multiplexer_2_out),
    .sel({in_3, in_2}));
  x4_universal_shift_reg x3_0 (
    .I(multiplexer_2_out), .Shift(in_2), .Left(in_3), .S(in_4), .Clk(in_5), .E(in_6), .R(in_7), .O0(O0),
    .O3(x3_0_o3[0]), .O(O[3:0]), .revO(revO[7:4]));

  // Notes on the sheet:
  //   Chaining these together is not quite as simple and requires some mux's
  //   Note however they are wired up more or less the same as the mux's from the x4 version
endmodule
