// Logisim project basicLogicGates.circ as structural Verilog: 3 circuits, main circuit basicGates
module basicGates (
  input  in_1,
  input  in_2,
  input  in_3,
  input  in_4,
  input  in_5,
  input  in_6,
  input  in_7,
  input  in_8,
  input  in_9,
  input  in_10,
  input  in_11,
  output out_12,
  output out_13,
  output out_14,
  output out_15,
  output out_16,
  output out_17
);

  not not_1 (out_12, in_2);
  and and_1 (out_14, in_4, in_6);
  or or_1 (out_16, in_8, in_10);
  nand nand_1 (out_13, in_1, in_3);
  nor nor_1 (out_15, in_5, in_7);
  xor xor_1 (out_17, in_9, in_11);
endmodule

module nandUniversal (
  input  in_1,
  input  in_2,
  input  in_3,
  input  in_4,
  input  in_5,
  input  in_6,
  input  in_7,
  input  in_8,
  input  in_9,
  output out_10,
  output out_11,
  output out_12,
  output out_13,
  output out_14
);

  wire nand_2_out, nand_3_out, nand_4_out, nand_5_out, nand_6_out, nand_9_out, nand_10_out, nand_11_out,
       nand_12_out;

  nand nand_1 (out_10, in_1, in_1);
  nand nand_2 (nand_2_out, in_4, in_5);
  nand nand_3 (nand_3_out, in_6, in_6);
  nand nand_4 (nand_4_out, in_7, in_7);
  nand nand_5 (nand_5_out, in_8, in_8);
  nand nand_6 (nand_6_out, in_9, in_9);
  nand nand_7 (out_12, nand_2_out, nand_2_out);
  nand nand_8 (out_13, nand_3_out, nand_4_out);
  nand nand_9 (nand_9_out, nand_5_out, nand_6_out);
  and and_1 (out_14, nand_9_out, nand_9_out);
  nand nand_10 (nand_10_out, in_2, in_3);
  nand nand_11 (nand_11_out, in_2, nand_10_out);
  nand nand_12 (nand_12_out, nand_10_out, in_3);
  nand nand_13 (out_11, nand_11_out, nand_12_out);

  // Notes on the sheet:
  //   Or
  //   Not
  //   And
  //   Nor
  //   Xor
endmodule

module norUniversal (
  input  in_1,
  input  in_2,
  input  in_3,
  input  in_4,
  input  in_5,
  input  in_6,
  input  in_7,
  input  in_8,
  input  in_9,
  output out_10,
  output out_11,
  output out_12,
  output out_13,
  output out_14
);

  wire nor_2_out, nor_3_out, nor_4_out, nor_5_out, nor_6_out, nor_9_out, nor_11_out, nor_12_out, nor_13_out,
       nor_14_out;

  nor nor_1 (out_10, in_1, in_1);
  nor nor_2 (nor_2_out, in_2, in_3);
  nor nor_3 (nor_3_out, in_6, in_6);
  nor nor_4 (nor_4_out, in_7, in_7);
  nor nor_5 (nor_5_out, in_8, in_8);
  nor nor_6 (nor_6_out, in_9, in_9);
  nor nor_7 (out_11, nor_2_out, nor_2_out);
  nor nor_8 (out_13, nor_3_out, nor_4_out);
  nor nor_9 (nor_9_out, nor_5_out, nor_6_out);
  nor nor_10 (out_14, nor_9_out, nor_9_out);
  nor nor_11 (nor_11_out, in_4, in_4);
  nor nor_12 (nor_12_out, in_5, in_5);
  nor nor_13 (nor_13_out, in_4, in_5);
  nor nor_14 (nor_14_out, nor_11_out, nor_12_out);
  nor nor_15 (out_12, nor_13_out, nor_14_out);

  // Notes on the sheet:
  //   Not
  //   Or
  //   And
  //   Nand
  //   Xor
endmodule
