// Logisim project decoders.circ as structural Verilog: 3 circuits, main circuit decoder_x1
module decoder_x1 (
  input  i,
  output o0,
  output o1
);

  not not_1 (o0, i);

  assign o1 = i;
endmodule

module decoder_x2 (
  input  [1:0] i,
  output o0,
  output o1,
  output o2,
  output o3
);

  wire decoder_x1_1_o0, decoder_x1_1_o1, decoder_x1_2_o0, decoder_x1_2_o1;

  decoder_x1 decoder_x1_1 (.i(i[0]), .o0(decoder_x1_1_o0), .o1(decoder_x1_1_o1));
  decoder_x1 decoder_x1_2 (.i(i[1]), .o0(decoder_x1_2_o0), .o1(decoder_x1_2_o1));
  and and_1 (o0, decoder_x1_1_o0, decoder_x1_2_o0);
  and and_2 (o1, decoder_x1_1_o1, decoder_x1_2_o0);
  and and_3 (o2, decoder_x1_1_o0, decoder_x1_2_o1);
  and and_4 (o3, decoder_x1_1_o1, decoder_x1_2_o1);
endmodule

module decoder_x3 (
  input  [2:0] i,
  output o0,
  output o1,
  output o2,
  output o3,
  output o4,
  output o5,
  output o6,
  output o7
);

  wire decoder_x1_1_o0, decoder_x1_1_o1, decoder_x2_1_o0, decoder_x2_1_o1, decoder_x2_1_o2, decoder_x2_1_o3;

  decoder_x2 decoder_x2_1 (
    .i(i[1:0]), .o0(decoder_x2_1_o0), .o1(decoder_x2_1_o1), .o2(decoder_x2_1_o2), .o3(decoder_x2_1_o3));
  decoder_x1 decoder_x1_1 (.i(i[2]), .o0(decoder_x1_1_o0), .o1(decoder_x1_1_o1));
  and and_1 (o0, decoder_x2_1_o0, decoder_x1_1_o0);
  and and_2 (o1, decoder_x2_1_o1, decoder_x1_1_o0);
  and and_3 (o2, decoder_x2_1_o2, decoder_x1_1_o0);
  and and_4 (o3, decoder_x2_1_o3, decoder_x1_1_o0);
  and and_5 (o4, decoder_x2_1_o0, decoder_x1_1_o1);
  and and_6 (o5, decoder_x2_1_o1, decoder_x1_1_o1);
  and and_7 (o6, decoder_x2_1_o2, decoder_x1_1_o1);
  and and_8 (o7, decoder_x2_1_o3, decoder_x1_1_o1);
endmodule
