// Logisim project fullAdder.circ as structural Verilog: 13 circuits, main circuit fullAdder_x1
module fullAdder_x1 (
  input  A,
  input  B,
  input  Cin,
  output Cout,
  output O
);

  wire and_1_out, and_2_out, xor_1_out;

  and and_1 (and_1_out, A, B);
  xor xor_1 (xor_1_out, A, B);
  and and_2 (and_2_out, xor_1_out, Cin);
  or or_1 (Cout, and_1_out, and_2_out);
  xor xor_2 (O, xor_1_out, Cin);
endmodule

module fullAdder_x2 (
  input  [1:0] A,
  input  [1:0] B,
  input  Cin,
  output Cout,
  output [1:0] O
);

  wire fulladder_x1_1_cout;

  fullAdder_x1 fulladder_x1_1 (.A(A[0]), .B(B[0]), .Cin(Cin), .Cout(fulladder_x1_1_cout), .O(O[0]));
  fullAdder_x1 fulladder_x1_2 (.A(A[1]), .B(B[1]), .Cin(fulladder_x1_1_cout), .Cout(Cout), .O(O[1]));
endmodule

module fullAdder_x4 (
  input  [3:0] A,
  input  [3:0] B,
  input  Cin,
  output Cout,
  output [3:0] O
);

  wire fulladder_x2_1_cout;

  fullAdder_x2 fulladder_x2_1 (.A(A[1:0]), .B(B[1:0]), .Cin(Cin), .Cout(fulladder_x2_1_cout), .O(O[1:0]));
  fullAdder_x2 fulladder_x2_2 (.A(A[3:2]), .B(B[3:2]), .Cin(fulladder_x2_1_cout), .Cout(Cout), .O(O[3:2]));
endmodule

module fullAdder_x8 (
  input  [7:0] A,
  input  [7:0] B,
  input  Cin,
  output Cout,
  output [7:0] O
);

  wire fulladder_x4_1_cout;

  fullAdder_x4 fulladder_x4_1 (.A(A[3:0]), .B(B[3:0]), .Cin(Cin), .Cout(fulladder_x4_1_cout), .O(O[3:0]));
  fullAdder_x4 fulladder_x4_2 (.A(A[7:4]), .B(B[7:4]), .Cin(fulladder_x4_1_cout), .Cout(Cout), .O(O[7:4]));
endmodule

module fullAdder_x16 (
  input  [15:0] A,
  input  [15:0] B,
  input  Cin,
  output Cout,
  output [15:0] O
);

  wire fulladder_x8_1_cout;

  fullAdder_x8 fulladder_x8_1 (.A(A[7:0]), .B(B[7:0]), .Cin(Cin), .Cout(fulladder_x8_1_cout), .O(O[7:0]));
  fullAdder_x8 fulladder_x8_2 (.A(A[15:8]), .B(B[15:8]), .Cin(fulladder_x8_1_cout), .Cout(Cout), .O(O[15:8]));
endmodule

module fullAdder_x32 (
  input  [31:0] A,
  input  [31:0] B,
  input  Cin,
  output Cout,
  output [31:0] O
);

  wire fulladder_x16_1_cout;

  fullAdder_x16 fulladder_x16_1 (.A(A[15:0]), .B(B[15:0]), .Cin(Cin), .Cout(fulladder_x16_1_cout), .O(O[15:0]));
  fullAdder_x16 fulladder_x16_2 (.A(A[31:16]), .B(B[31:16]), .Cin(fulladder_x16_1_cout), .Cout(Cout), .O(O[31:16]));
endmodule

module lookAheadAdder_x1 (
  input  A,
  input  B,
  input  Cin,
  output G,
  output P,
  output O
);

  and and_1 (G, A, B);
  xor xor_1 (P, A, B);
  xor xor_2 (O, P, Cin);
endmodule

module lookAheadAdder_x2 (
  input  [1:0] A,
  input  [1:0] B,
  input  Cin,
  output out_4,
  output out_5,
  output [1:0] out_6
);

  wire and_1_out, lookaheadadder_x1_1_g, lookaheadadder_x1_1_p, or_1_out;

  lookAheadAdder_x1 lookaheadadder_x1_1 (
    .A(A[0]), .B(B[0]), .Cin(Cin), .G(lookaheadadder_x1_1_g), .P(lookaheadadder_x1_1_p), .O(out_6[0]));
  and and_1 (and_1_out, lookaheadadder_x1_1_p, Cin);
  or or_1 (or_1_out, lookaheadadder_x1_1_g, and_1_out);
  lookAheadAdder_x1 lookaheadadder_x1_2 (.A(A[1]), .B(B[1]), .Cin(or_1_out), .G(out_4), .P(out_5), .O(out_6[1]));
endmodule

module lookAheadAdder_x4 (
  input  [3:0] A,
  input  [3:0] B,
  input  Cin,
  output [3:0] O,
  output Cout
);

  wire and_1_out, and_2_out, and_3_out, and_4_out, and_5_out, and_6_out, and_7_out, and_8_out, and_9_out,
       and_10_out, and_11_out, and_12_out, and_13_out, and_14_out, and_15_out, and_16_out, and_17_out,
       and_18_out, and_19_out, and_20_out, lookaheadadder_x1_1_g, lookaheadadder_x1_1_p,
       lookaheadadder_x1_2_g, lookaheadadder_x1_2_p, lookaheadadder_x1_3_g, lookaheadadder_x1_3_p,
       lookaheadadder_x1_4_g, lookaheadadder_x1_4_p, or_1_out, or_2_out, or_3_out, or_4_out, or_5_out,
       or_6_out, or_7_out, or_8_out, or_10_out;

  lookAheadAdder_x1 lookaheadadder_x1_1 (
    .A(A[0]), .B(B[0]), .Cin(Cin), .G(lookaheadadder_x1_1_g), .P(lookaheadadder_x1_1_p), .O(O[0]));
  or or_1 (or_1_out, lookaheadadder_x1_1_g, and_1_out);
  and and_1 (and_1_out, lookaheadadder_x1_1_p, Cin);
  lookAheadAdder_x1 lookaheadadder_x1_2 (
    .A(A[1]), .B(B[1]), .Cin(or_1_out), .G(lookaheadadder_x1_2_g), .P(lookaheadadder_x1_2_p), .O(O[1]));
  or or_2 (or_2_out, lookaheadadder_x1_2_g, and_2_out);
  and and_2 (and_2_out, lookaheadadder_x1_2_p, lookaheadadder_x1_1_g);
  or or_3 (or_3_out, or_2_out, and_3_out);
  and and_3 (and_3_out, lookaheadadder_x1_2_p, and_4_out);
  and and_4 (and_4_out, lookaheadadder_x1_1_p, Cin);
  lookAheadAdder_x1 lookaheadadder_x1_3 (
    .A(A[2]), .B(B[2]), .Cin(or_3_out), .G(lookaheadadder_x1_3_g), .P(lookaheadadder_x1_3_p), .O(O[2]));
  or or_4 (or_4_out, or_5_out, or_6_out);
  or or_5 (or_5_out, lookaheadadder_x1_3_g, and_5_out);
  and and_5 (and_5_out, lookaheadadder_x1_3_p, lookaheadadder_x1_2_g);
  and and_6 (and_6_out, lookaheadadder_x1_3_p, and_7_out);
  and and_7 (and_7_out, lookaheadadder_x1_2_p, lookaheadadder_x1_1_g);
  or or_6 (or_6_out, and_6_out, and_8_out);
  and and_8 (and_8_out, and_9_out, and_10_out);
  and and_9 (and_9_out, lookaheadadder_x1_3_p, lookaheadadder_x1_2_p);
  and and_10 (and_10_out, lookaheadadder_x1_1_p, Cin);
  lookAheadAdder_x1 lookaheadadder_x1_4 (
    .A(A[3]), .B(B[3]), .Cin(or_4_out), .G(lookaheadadder_x1_4_g), .P(lookaheadadder_x1_4_p), .O(O[3]));
  or or_7 (or_7_out, or_8_out, or_10_out);
  or or_8 (or_8_out, lookaheadadder_x1_4_g, and_11_out);
  and and_11 (and_11_out, lookaheadadder_x1_4_p, lookaheadadder_x1_3_g);
  and and_12 (and_12_out, lookaheadadder_x1_4_p, and_14_out);
  or or_9 (Cout, or_7_out, and_16_out);
  or or_10 (or_10_out, and_12_out, and_13_out);
  and and_13 (and_13_out, and_15_out, and_19_out);
  and and_14 (and_14_out, lookaheadadder_x1_3_p, lookaheadadder_x1_2_g);
  and and_15 (and_15_out, lookaheadadder_x1_4_p, lookaheadadder_x1_3_p);
  and and_16 (and_16_out, lookaheadadder_x1_4_p, and_17_out);
  and and_17 (and_17_out, and_18_out, and_20_out);
  and and_18 (and_18_out, lookaheadadder_x1_3_p, lookaheadadder_x1_2_p);
  and and_19 (and_19_out, lookaheadadder_x1_2_p, lookaheadadder_x1_1_g);
  and and_20 (and_20_out, lookaheadadder_x1_1_p, Cin);
endmodule

module claUnit_x4 (
  input  Cin,
  input  P0,
  input  G0,
  input  P1,
  input  G1,
  input  P2,
  input  G2,
  input  P3,
  input  G3,
  output PG,
  output C1,
  output C2,
  output C3,
  output Cout4,
  output GG
);

  wire and_1_out, and_2_out, and_3_out, and_4_out, and_5_out, and_6_out, and_7_out, and_8_out, and_9_out,
       and_10_out, and_11_out, and_13_out, or_2_out, or_4_out, or_5_out, or_7_out, or_8_out;

  and and_1 (and_1_out, Cin, P0);
  or or_1 (C1, and_1_out, G0);
  and and_2 (and_2_out, and_1_out, P1);
  and and_3 (and_3_out, G0, P1);
  or or_2 (or_2_out, and_3_out, G1);
  or or_3 (C2, and_2_out, or_2_out);
  and and_4 (and_4_out, and_2_out, P2);
  and and_5 (and_5_out, and_3_out, P2);
  and and_6 (and_6_out, G1, P2);
  or or_4 (or_4_out, and_4_out, and_5_out);
  or or_5 (or_5_out, and_6_out, G2);
  or or_6 (C3, or_4_out, or_5_out);
  and and_7 (and_7_out, and_4_out, P3);
  and and_8 (and_8_out, and_5_out, P3);
  and and_9 (and_9_out, G2, P3);
  and and_10 (and_10_out, and_6_out, P3);
  or or_7 (or_7_out, and_9_out, G3);
  or or_8 (or_8_out, and_10_out, or_7_out);
  or or_9 (GG, and_8_out, or_8_out);
  or or_10 (Cout4, and_7_out, GG);
  and and_11 (and_11_out, P0, P1);
  and and_12 (PG, and_11_out, and_13_out);
  and and_13 (and_13_out, P2, P3);
endmodule

module cla_x4 (
  input  [3:0] A,
  input  [3:0] B,
  input  Cin,
  output [3:0] O,
  output Cout,
  output GG,
  output PG
);

  wire claunit_x4_1_c1, claunit_x4_1_c2, claunit_x4_1_c3, lookaheadadder_x1_1_g, lookaheadadder_x1_1_p,
       lookaheadadder_x1_2_g, lookaheadadder_x1_2_p, lookaheadadder_x1_3_g, lookaheadadder_x1_3_p,
       lookaheadadder_x1_4_g, lookaheadadder_x1_4_p;

  lookAheadAdder_x1 lookaheadadder_x1_1 (
    .A(A[0]), .B(B[0]), .Cin(Cin), .G(lookaheadadder_x1_1_g), .P(lookaheadadder_x1_1_p), .O(O[0]));
  lookAheadAdder_x1 lookaheadadder_x1_2 (
    .A(A[1]), .B(B[1]), .Cin(claunit_x4_1_c1), .G(lookaheadadder_x1_2_g), .P(lookaheadadder_x1_2_p), .O(O[1]));
  lookAheadAdder_x1 lookaheadadder_x1_3 (
    .A(A[2]), .B(B[2]), .Cin(claunit_x4_1_c2), .G(lookaheadadder_x1_3_g), .P(lookaheadadder_x1_3_p), .O(O[2]));
  claUnit_x4 claunit_x4_1 (
    .G3(lookaheadadder_x1_4_g), .Cin(Cin), .P0(lookaheadadder_x1_1_p), .G0(lookaheadadder_x1_1_g),
    .P1(lookaheadadder_x1_2_p), .G1(lookaheadadder_x1_2_g), .P2(lookaheadadder_x1_3_p),
    .G2(lookaheadadder_x1_3_g), .P3(lookaheadadder_x1_4_p), .GG(GG), .PG(PG), .C1(claunit_x4_1_c1),
    .C2(claunit_x4_1_c2), .C3(claunit_x4_1_c3), .Cout4(Cout));
  lookAheadAdder_x1 lookaheadadder_x1_4 (
    .A(A[3]), .B(B[3]), .Cin(claunit_x4_1_c3), .G(lookaheadadder_x1_4_g), .P(lookaheadadder_x1_4_p), .O(O[3]));
endmodule

module cla_x16 (
  input  [15:0] A,
  input  [15:0] B,
  input  Cin,
  output [15:0] O,
  output Cout,
  output GG,
  output PG
);

  wire cla_x4_1_gg, cla_x4_1_pg, cla_x4_2_gg, cla_x4_2_pg, cla_x4_3_gg, cla_x4_3_pg, cla_x4_4_gg,
       cla_x4_4_pg, claunit_x4_1_c1, claunit_x4_1_c2, claunit_x4_1_c3;

  cla_x4 cla_x4_1 (.A(A[3:0]), .B(B[3:0]), .Cin(Cin), .O(O[3:0]), .GG(cla_x4_1_gg), .PG(cla_x4_1_pg));  // open: Cout
  cla_x4 cla_x4_2 (
    .A(A[7:4]), .B(B[7:4]), .Cin(claunit_x4_1_c1), .O(O[7:4]), .GG(cla_x4_2_gg), .PG(cla_x4_2_pg));  // open: Cout
  cla_x4 cla_x4_3 (
    .A(A[11:8]), .B(B[11:8]), .Cin(claunit_x4_1_c2), .O(O[11:8]), .GG(cla_x4_3_gg), .PG(cla_x4_3_pg));  // open: Cout
  claUnit_x4 claunit_x4_1 (
    .G3(cla_x4_4_gg), .Cin(Cin), .P0(cla_x4_1_pg), .G0(cla_x4_1_gg), .P1(cla_x4_2_pg), .G1(cla_x4_2_gg),
    .P2(cla_x4_3_pg), .G2(cla_x4_3_gg), .P3(cla_x4_4_pg), .GG(GG), .PG(PG), .C1(claunit_x4_1_c1),
    .C2(claunit_x4_1_c2), .C3(claunit_x4_1_c3), .Cout4(Cout));
  cla_x4 cla_x4_4 (
    .A(A[15:12]), .B(B[15:12]), .Cin(claunit_x4_1_c3), .O(O[15:12]), .GG(cla_x4_4_gg), .PG(cla_x4_4_pg));  // open: Cout
endmodule

module cla_x32 (
  input  [31:0] in_1,
  input  [31:0] in_2,
  input  in_3,
  output [31:0] out_4,
  output out_5
);

  wire and_1_out, cla_x16_1_gg, cla_x16_1_pg, or_1_out;

  cla_x16 cla_x16_1 (
    .A(in_1[15:0]), .B(in_2[15:0]), .Cin(in_3), .O(out_4[15:0]), .GG(cla_x16_1_gg), .PG(cla_x16_1_pg));  // open: Cout
  and and_1 (and_1_out, cla_x16_1_pg, in_3);
  or or_1 (or_1_out, cla_x16_1_gg, and_1_out);
  cla_x16 cla_x16_2 (.A(in_1[31:16]), .B(in_2[31:16]), .Cin(or_1_out), .O(out_4[31:16]), .Cout(out_5));  // open: GG, PG
endmodule
