// Logisim project mux.circ as structural Verilog: 4 circuits, main circuit mux_2x1
module mux_2x1 (
  input  s0,
  input  i0,
  input  i1,
  output o
);

  wire and_1_out, and_2_out, not_1_out;

  not not_1 (not_1_out, s0);
  and and_1 (and_1_out, i0, not_1_out);
  and and_2 (and_2_out, s0, i1);
  or or_1 (o, and_1_out, and_2_out);
endmodule

module mux_4x1 (
  input  [1:0] s0_1,
  input  i0,
  input  i1,
  input  i2,
  input  i3,
  output o
);

  wire mux_2x1_1_o, mux_2x1_2_o;

  mux_2x1 mux_2x1_1 (.s0(s0_1[0]), .i0(i0), .i1(i1), .o(mux_2x1_1_o));
  mux_2x1 mux_2x1_2 (.s0(s0_1[0]), .i0(i2), .i1(i3), .o(mux_2x1_2_o));
  mux_2x1 mux_2x1_3 (.s0(s0_1[1]), .i0(mux_2x1_1_o), .i1(mux_2x1_2_o), .o(o));
endmodule

module mux_8x1 (
  input  [2:0] s0_2,
  input  i0,
  input  i1,
  input  i2,
  input  i3,
  input  i4,
  input  i5,
  input  i6,
  input  i7,
  output o
);

  wire mux_4x1_1_o, mux_4x1_2_o;

  mux_4x1 mux_4x1_1 (.s0_1(s0_2[1:0]), .i0(i0), .i1(i1), .i2(i2), .i3(i3), .o(mux_4x1_1_o));
  mux_4x1 mux_4x1_2 (.s0_1(s0_2[1:0]), .i0(i4), .i1(i5), .i2(i6), .i3(i7), .o(mux_4x1_2_o));
  mux_2x1 mux_2x1_1 (.s0(s0_2[2]), .i0(mux_4x1_1_o), .i1(mux_4x1_2_o), .o(o));
endmodule

module mux_2x2 (
  input  s0,
  input  [1:0] i0,
  input  [1:0] i1,
  output [1:0] o
);

  mux_2x1 mux_2x1_1 (.s0(s0), .i0(i0[0]), .i1(i1[0]), .o(o[0]));
  mux_2x1 mux_2x1_2 (.s0(s0), .i0(i0[1]), .i1(i1[1]), .o(o[1]));
endmodule
